// Logisim project laboratiorio_C00.circ as structural Verilog: 2 circuits, main circuit main
module main (
  input  Ma,
  input  Mb,
  output Mo1,
  output Mo2,
  output Mo3
);

  wire block1_1_f, block1_1_f2, block1_1_f3, block1_2_f3;

  Block1 block1_1 (.A(Ma), .B(Mb), .F(block1_1_f), .F2(block1_1_f2), .F3(block1_1_f3));
  Block1 block1_2 (.A(block1_1_f), .B(block1_1_f2), .F(Mo1), .F2(Mo2), .F3(block1_2_f3));
  or or_1 (Mo3, block1_2_f3, block1_1_f3);
endmodule

module Block1 (
  input  A,
  input  B,
  output F,
  output F2,
  output F3
);

  and AND1 (F, A, B);
  or OR1 (F2, A, B);
  or OR3 (F3, A, B);
endmodule
