// Logisim project Laboratorio2.circ as structural Verilog: 10 circuits, main circuit main
module main (
);

  wire clock_1_out, Reset_out;
  wire [1:0] joystick_1_x;
  wire [3:0] lvl;
  wire [13:0] Past, Trapped;
  wire [15:0] controller_1_control_move, controller_1_d1_display, controller_1_d16_display,
       controller_1_out_5, controller_1_out_6, controller_1_out_7, controller_1_out_8, controller_1_out_9,
       controller_1_out_10, controller_1_out_11, controller_1_out_12, controller_1_out_13,
       controller_1_out_14, controller_1_out_15, controller_1_out_16, controller_1_out_17,
       controller_1_out_18;

  Button Reset (.out(Reset_out));
  Joystick #(.bits(2)) joystick_1 (.x(joystick_1_x));  // open: y
  Clock clock_1 (.out(clock_1_out));
  Controller controller_1 (
    .Reset(Reset_out), .control(joystick_1_x), .clk(clock_1_out), .d1_display(controller_1_d1_display),
    .out_5(controller_1_out_5), .out_6(controller_1_out_6), .out_7(controller_1_out_7),
    .out_8(controller_1_out_8), .out_9(controller_1_out_9), .out_10(controller_1_out_10),
    .out_11(controller_1_out_11), .out_12(controller_1_out_12), .out_13(controller_1_out_13),
    .out_14(controller_1_out_14), .out_15(controller_1_out_15), .out_16(controller_1_out_16),
    .out_17(controller_1_out_17), .out_18(controller_1_out_18), .d16_display(controller_1_d16_display),
    .Control_Move(controller_1_control_move), .trapped(Trapped), .past(Past), .Level(lvl));
  DotMatrix #(.dotshape("circle"), .inputtype("row"), .matrixcols(16), .matrixrows(16)) dotmatrix_1 (
    .row0(controller_1_d1_display), .row1(controller_1_out_5), .row2(controller_1_out_6),
    .row3(controller_1_out_7), .row4(controller_1_out_8), .row5(controller_1_out_9),
    .row6(controller_1_out_10), .row7(controller_1_out_11), .row8(controller_1_out_12),
    .row9(controller_1_out_13), .row10(controller_1_out_14), .row11(controller_1_out_15),
    .row12(controller_1_out_16), .row13(controller_1_out_17), .row14(controller_1_out_18),
    .row15(controller_1_d16_display));
  DotMatrix #(.inputtype("row"), .matrixcols(16), .matrixrows(1)) dotmatrix_2 (.row0(controller_1_control_move));
  _7_Segment_Display #(.decimalPoint("false")) u_7_segment_display_1 (
    .g(Trapped[13]), .f(Trapped[12]), .a(Trapped[7]), .b(Trapped[8]), .e(Trapped[11]), .d(Trapped[10]),
    .c(Trapped[9]));
  LED led_1 (.in(lvl[0]));
  LED led_2 (.in(lvl[1]));
  LED led_3 (.in(lvl[2]));
  _7_Segment_Display #(.decimalPoint("false")) u_7_segment_display_2 (
    .g(Past[13]), .f(Past[12]), .a(Past[7]), .b(Past[8]), .e(Past[11]), .d(Past[10]), .c(Past[9]));
  LED led_4 (.in(lvl[3]));
  _7_Segment_Display #(.decimalPoint("false")) u_7_segment_display_3 (
    .g(Trapped[6]), .f(Trapped[5]), .a(Trapped[0]), .b(Trapped[1]), .e(Trapped[4]), .d(Trapped[3]),
    .c(Trapped[2]));
  _7_Segment_Display #(.decimalPoint("false")) u_7_segment_display_4 (
    .g(Past[6]), .f(Past[5]), .a(Past[0]), .b(Past[1]), .e(Past[4]), .d(Past[3]), .c(Past[2]));

  // Notes on the sheet:
  //   "Catch a falling star"
  //   Levels
  //   1
  //   2
  //   3
  //   4
  //   Estrellas Atrapadas
  //   Estrellas Pasadas
endmodule

module BCD7SEG (
  input  min,
  input  in_2,
  input  in_3,
  input  max,
  output a,
  output b,
  output c,
  output d,
  output e,
  output f,
  output g
);

  wire and_1_out, and_2_out, and_3_out, and_4_out, and_5_out, and_6_out, and_7_out, and_8_out, and_9_out,
       and_10_out, and_11_out, and_12_out, and_13_out, and_14_out, and_15_out, and_16_out, and_17_out,
       and_18_out, and_19_out, and_20_out, and_21_out, and_22_out, and_23_out, and_24_out, and_25_out,
       not_1_out, not_2_out, not_3_out, not_4_out;

  not not_1 (not_1_out, max);
  not not_2 (not_2_out, in_3);
  not not_3 (not_3_out, in_2);
  not not_4 (not_4_out, min);
  and and_1 (and_1_out, not_1_out, not_2_out, not_4_out);
  and and_2 (and_2_out, not_1_out, in_2);
  and and_3 (and_3_out, not_1_out, in_3, min);
  and and_4 (and_4_out, max, not_2_out, not_3_out);
  and and_5 (and_5_out, not_1_out, not_2_out);
  and and_6 (and_6_out, not_1_out, not_3_out, not_4_out);
  and and_7 (and_7_out, not_2_out, not_3_out);
  and and_8 (and_8_out, not_1_out, in_2, min);
  and and_9 (and_9_out, not_2_out, not_3_out);
  and and_10 (and_10_out, not_1_out, min);
  and and_11 (and_11_out, not_1_out, in_3);
  and and_12 (and_12_out, not_2_out, not_3_out, not_4_out);
  and and_13 (and_13_out, not_1_out, not_2_out, in_2);
  and and_14 (and_14_out, not_1_out, in_2, not_4_out);
  and and_15 (and_15_out, not_1_out, in_3, not_3_out, min);
  and and_16 (and_16_out, not_2_out, not_3_out, not_4_out);
  and and_17 (and_17_out, not_1_out, in_2, not_4_out);
  and and_18 (and_18_out, not_1_out, not_3_out, not_4_out);
  and and_19 (and_19_out, not_1_out, in_3, not_3_out);
  and and_20 (and_20_out, not_1_out, in_3, not_4_out);
  and and_21 (and_21_out, max, not_2_out, not_3_out);
  and and_22 (and_22_out, not_1_out, not_2_out, in_2);
  and and_23 (and_23_out, not_1_out, in_3, not_3_out);
  and and_24 (and_24_out, not_1_out, in_3, not_4_out);
  and and_25 (and_25_out, max, not_2_out, not_3_out);
  or or_1 (a, and_1_out, and_2_out, and_3_out, and_4_out);
  or or_2 (b, and_5_out, and_6_out, and_7_out, and_8_out);
  or or_3 (c, and_9_out, and_10_out, and_11_out);
  or or_4 (d, and_12_out, and_13_out, and_14_out, and_15_out);
  or or_5 (e, and_16_out, and_17_out);
  or or_6 (f, and_18_out, and_19_out, and_20_out, and_21_out);
  or or_7 (g, and_22_out, and_23_out, and_24_out, and_25_out);
endmodule

module BCD7SEGx2 (
  input  [6:0] inBCDx2,
  output Dg,
  output Df,
  output De,
  output Dd,
  output Dc,
  output Db,
  output Da,
  output Ug,
  output Uf,
  output Ue,
  output Ud,
  output Uc,
  output Ub,
  output Ua
);

  wire [6:0] divider_1_out, divider_1_rem;

  Divider #(.width(7)) divider_1 (
    .a(inBCDx2), .b(7'b0001010), .out(divider_1_out), .rem(divider_1_rem));  // open: upper
  // Probe on divider_1_rem
  // Probe on divider_1_out
  _7_Segment_Display u_7_segment_display_1 (.g(Dg), .f(Df), .a(Da), .b(Db), .e(De), .d(Dd), .c(Dc));  // open: dp
  _7_Segment_Display u_7_segment_display_2 (.g(Ug), .f(Uf), .a(Ua), .b(Ub), .e(Ue), .d(Ud), .c(Uc));  // open: dp
  BCD7SEG Decenas (
    .min(divider_1_out[0]), .in_2(divider_1_out[1]), .in_3(divider_1_out[2]), .max(divider_1_out[3]), .a(Da),
    .b(Db), .c(Dc), .d(Dd), .e(De), .f(Df), .g(Dg));
  BCD7SEG Unidades (
    .min(divider_1_rem[0]), .in_2(divider_1_rem[1]), .in_3(divider_1_rem[2]), .max(divider_1_rem[3]), .a(Ua),
    .b(Ub), .c(Uc), .d(Ud), .e(Ue), .f(Uf), .g(Ug));

  // Other names for the same wires on the sheet: a = Da; a1 = Ua; b = Db; b1 = Ub; c = Dc; c1 = Uc; d = Dd; d1 = Ud;
  //   e = De; e1 = Ue; f = Df; f1 = Uf; g = Dg; g1 = Ug
endmodule

module ContadorUnitario_trapped (
  input  push,
  input  Reset,
  output [1:0] outLevel,
  output [6:0] Unidades,
  output [6:0] Decenas,
  output GameWin
);

  wire and_2_out, and_3_out, and_4_out, not_1_out, not_2_out, not_3_out, not_4_out, not_5_out, not_6_out,
       not_7_out, not_8_out, not_9_out, or_1_out, t_ff_1_qn, t_ff_2_qn, t_ff_3_qn, t_ff_4_qn, t_ff_5_qn,
       t_ff_7_qn;
  wire [6:0] t_ff_1_q;

  T_Flip_Flop t_ff_1 (.T(1'b1), .clk(push), .Q(t_ff_1_q[0]), .Qn(t_ff_1_qn), .reset(Reset));  // open: preset
  and and_1 (GameWin, t_ff_1_q[0], t_ff_1_q[1], t_ff_1_q[2], t_ff_1_q[3], t_ff_1_q[4], t_ff_1_q[5]);
  BCD7SEGx2 bcd7segx2_1 (
    .inBCDx2(t_ff_1_q), .Dg(Decenas[6]), .Df(Decenas[5]), .De(Decenas[4]), .Dd(Decenas[3]), .Dc(Decenas[2]),
    .Db(Decenas[1]), .Da(Decenas[0]), .Ug(Unidades[6]), .Uf(Unidades[5]), .Ue(Unidades[4]), .Ud(Unidades[3]),
    .Uc(Unidades[2]), .Ub(Unidades[1]), .Ua(Unidades[0]));
  T_Flip_Flop t_ff_2 (.T(1'b1), .clk(t_ff_1_qn), .Q(t_ff_1_q[1]), .Qn(t_ff_2_qn), .reset(Reset));  // open: preset
  T_Flip_Flop t_ff_3 (.T(1'b1), .clk(t_ff_2_qn), .Q(t_ff_1_q[2]), .Qn(t_ff_3_qn), .reset(Reset));  // open: preset
  T_Flip_Flop t_ff_4 (.T(1'b1), .clk(t_ff_3_qn), .Q(t_ff_1_q[3]), .Qn(t_ff_4_qn), .reset(Reset));  // open: preset
  not not_1 (not_1_out, t_ff_1_q[2]);
  not not_2 (not_2_out, t_ff_1_q[3]);
  not not_3 (not_3_out, t_ff_1_q[3]);
  T_Flip_Flop t_ff_5 (.T(1'b1), .clk(t_ff_4_qn), .Q(t_ff_1_q[4]), .Qn(t_ff_5_qn), .reset(Reset));  // open: preset
  T_Flip_Flop t_ff_6 (.T(1'b1), .clk(t_ff_5_qn), .Q(t_ff_1_q[5]), .reset(Reset));  // open: Qn, preset
  not not_4 (not_4_out, t_ff_1_q[4]);
  not not_5 (not_5_out, t_ff_1_q[4]);
  not not_6 (not_6_out, t_ff_1_q[4]);
  _7_Segment_Display u_7_segment_display_1 (
    .g(Decenas[6]), .f(Decenas[5]), .a(Decenas[0]), .b(Decenas[1]), .e(Decenas[4]), .d(Decenas[3]),
    .c(Decenas[2]));  // open: dp
  not not_7 (not_7_out, t_ff_1_q[5]);
  not not_8 (not_8_out, t_ff_1_q[5]);
  not not_9 (not_9_out, t_ff_1_q[5]);
  _7_Segment_Display u_7_segment_display_2 (
    .g(Unidades[6]), .f(Unidades[5]), .a(Unidades[0]), .b(Unidades[1]), .e(Unidades[4]), .d(Unidades[3]),
    .c(Unidades[2]));  // open: dp
  and and_2 (and_2_out, t_ff_1_q[0], t_ff_1_q[1], not_1_out, not_2_out, not_4_out, not_7_out);
  and and_3 (and_3_out, t_ff_1_q[0], t_ff_1_q[1], t_ff_1_q[2], not_3_out, not_5_out, not_8_out);
  and and_4 (and_4_out, t_ff_1_q[0], t_ff_1_q[1], t_ff_1_q[2], t_ff_1_q[3], not_6_out, not_9_out);
  or or_1 (or_1_out, and_2_out, and_3_out, and_4_out);
  T_Flip_Flop t_ff_7 (.T(1'b1), .clk(or_1_out), .Q(outLevel[0]), .Qn(t_ff_7_qn), .reset(Reset));  // open: preset
  T_Flip_Flop t_ff_8 (.T(1'b1), .clk(t_ff_7_qn), .Q(outLevel[1]), .reset(Reset));  // open: Qn, preset
  // Probe on outLevel

  // Other names for the same wires on the sheet: a = Decenas[0]; b = Decenas[1]; c = Decenas[2]; d = Decenas[3];
  //   e = Decenas[4]; f = Decenas[5]; g = Decenas[6]; Rst = Reset; a1 = Unidades[0]; b1 = Unidades[1];
  //   c1 = Unidades[2]; d1 = Unidades[3]; e1 = Unidades[4]; f1 = Unidades[5]; g1 = Unidades[6]; Win = GameWin
endmodule

module Controller (
  input  Reset,
  input  [1:0] control,
  input  clk,
  output [15:0] d1_display,
  output [15:0] out_5,
  output [15:0] out_6,
  output [15:0] out_7,
  output [15:0] out_8,
  output [15:0] out_9,
  output [15:0] out_10,
  output [15:0] out_11,
  output [15:0] out_12,
  output [15:0] out_13,
  output [15:0] out_14,
  output [15:0] out_15,
  output [15:0] out_16,
  output [15:0] out_17,
  output [15:0] out_18,
  output [15:0] d16_display,
  output [15:0] Control_Move,
  output [13:0] trapped,
  output [13:0] past,
  output [3:0] Level
);

  wire and_2_out, clk_t, clkF, comparator_1_eq, comparator_2_eq, d_ff_1_q, d_ff_2_q, gameOver, gameWin,
       not_1_out, not_2_out;
  wire [1:0] lvl;

  Comparator #(.width(16)) comparator_1 (.a(Control_Move), .b(d16_display), .eq(comparator_1_eq));  // open: gt, lt
  Comparator #(.width(16)) comparator_2 (.a({16{1'b0}}), .b(d16_display), .eq(comparator_2_eq));  // open: gt, lt
  D_Flip_Flop d_ff_1 (.D(comparator_1_eq), .clk(clkF), .Q(d_ff_1_q));  // open: Qn, preset, reset
  not not_1 (not_1_out, comparator_1_eq);
  not not_2 (not_2_out, comparator_2_eq);
  and and_1 (clk_t, clk, ~gameOver, ~gameWin);  // AND_Gate
  D_Flip_Flop d_ff_2 (.D(and_2_out), .clk(clkF), .Q(d_ff_2_q));  // open: Qn, preset, reset
  and and_2 (and_2_out, not_1_out, not_2_out);
  fallingStar fallingstar_1 (
    .rst(Reset), .clk(clkF), .init(d1_display), .out_4(out_5), .out_5(out_6), .out_6(out_7), .out_7(out_8),
    .out_8(out_9), .out_9(out_10), .out_10(out_11), .out_11(out_12), .out_12(out_13), .out_13(out_14),
    .out_14(out_15), .out_15(out_16), .out_16(out_17), .out_17(out_18), .fin(d16_display));
  MoveControl movecontrol_1 (.Reset(Reset), .Control_Joystick(control), .Clk(clk_t), .Ctlr(Control_Move));
  ContadorUnitario_trapped contadorunitario_trapped_1 (
    .Decenas(trapped[13:7]), .Unidades(trapped[6:0]), .GameWin(gameWin), .outLevel(lvl), .Reset(Reset),
    .push(d_ff_1_q));
  ContadorUnitario_Past contadorunitario_past_1 (
    .push(d_ff_2_q), .Reset(Reset), .GameOver(gameOver), .Unidades(past[6:0]), .Decenas(past[13:7]));
  Decoder #(.select(2)) decoder_1 (
    .out0(Level[0]), .out1(Level[1]), .out2(Level[2]), .out3(Level[3]), .sel(lvl));  // open: en
  freq_devider freq_devider_1 (.CLk(clk_t), .Rst(Reset), .inLevel(lvl), .outLevel(clkF));

  // Other names for the same wires on the sheet: ctrl[15:0] = Control_Move; limite[15:0] = d16_display; Rst = Reset

  // Notes on the sheet:
  //   Control de estrellas atrapadas o pasadas
  //   Generador de estrellas aletorias y registro de caida
  //   Control de movimiento del joystick
  //   Contadores
  //   Contador de estrellas atrapadas
  //   Contador de estrellas pasadas
  //   Dividor de frecuencia por niveles
endmodule

module fallingStar (
  input  rst,
  input  clk,
  output [15:0] init,
  output [15:0] out_4,
  output [15:0] out_5,
  output [15:0] out_6,
  output [15:0] out_7,
  output [15:0] out_8,
  output [15:0] out_9,
  output [15:0] out_10,
  output [15:0] out_11,
  output [15:0] out_12,
  output [15:0] out_13,
  output [15:0] out_14,
  output [15:0] out_15,
  output [15:0] out_16,
  output [15:0] out_17,
  output [15:0] fin
);

  wire [1:0] counter_1_q;
  wire [3:0] random_1_out;
  wire [15:0] decoder_1_out0, multiplexer_1_out;

  Random #(.width(4)) random_1 (.clr(rst), .clk(clk), .out(random_1_out));  // open: next
  Decoder #(.select(4)) decoder_1 (
    .out0(decoder_1_out0[0]), .out1(decoder_1_out0[1]), .out2(decoder_1_out0[2]), .out3(decoder_1_out0[3]),
    .out4(decoder_1_out0[4]), .out5(decoder_1_out0[5]), .out6(decoder_1_out0[6]), .out7(decoder_1_out0[7]),
    .out8(decoder_1_out0[8]), .out9(decoder_1_out0[9]), .out10(decoder_1_out0[10]),
    .out11(decoder_1_out0[11]), .out12(decoder_1_out0[12]), .out13(decoder_1_out0[13]),
    .out14(decoder_1_out0[14]), .out15(decoder_1_out0[15]), .sel(random_1_out));  // open: en
  // Probe on random_1_out
  Multiplexer #(.enable("false"), .select(2), .width(16)) multiplexer_1 (
    .in0(decoder_1_out0), .in1({16{1'b0}}), .in2({16{1'b0}}), .in3({16{1'b0}}), .out(multiplexer_1_out),
    .sel(counter_1_q));
  Counter #(.max('h3), .width(2)) counter_1 (.Q(counter_1_q), .clk(clk));  // open: load, D, count, carry, up, clr
  // Shift_Register #(.length(16), .width(16)) shift_register_1: pin names not known; wires that end beside it: rst, clk, multiplexer_1_out, init, out_4, out_5, out_6, out_7, out_8, out_9, out_10, out_11, out_12, out_13, out_14
endmodule

module freq_devider (
  input  CLk,
  input  Rst,
  input  [1:0] inLevel,
  output outLevel
);

  wire t_ff_1_q;
  wire [3:0] value;

  T_Flip_Flop t_ff_1 (.T(1'b1), .clk(CLk), .Q(t_ff_1_q), .reset(Rst));  // open: Qn, preset
  T_Flip_Flop t_ff_2 (.T(1'b1), .clk(t_ff_1_q), .Q(value[3]), .reset(Rst));  // open: Qn, preset
  T_Flip_Flop t_ff_3 (.T(1'b1), .clk(value[3]), .Q(value[2]), .reset(Rst));  // open: Qn, preset
  // Probe on outLevel
  Multiplexer #(.enable("false"), .select(2)) multiplexer_1 (
    .in0(value[0]), .in1(value[1]), .in2(value[2]), .in3(value[3]), .out(outLevel), .sel(inLevel));
  T_Flip_Flop t_ff_4 (.T(1'b1), .clk(value[2]), .Q(value[1]), .reset(Rst));  // open: Qn, preset
  T_Flip_Flop t_ff_5 (.T(1'b1), .clk(value[1]), .Q(value[0]), .reset(Rst));  // open: Qn, preset
endmodule

module LevelControl (
  input  Clk,
  input  inLevel,
  input  Reset,
  output [1:0] outLevel,
  output Z
);

  wire J1, K0;

  and and_1 (J1, outLevel[0], inLevel);
  and and_2 (K0, outLevel[1], inLevel);
  J_K_Flip_Flop j_k_ff_1 (.J(J1), .K(inLevel), .clk(Clk), .Q(outLevel[1]), .reset(Reset));  // open: Qn, preset
  J_K_Flip_Flop j_k_ff_2 (.J(inLevel), .K(K0), .clk(Clk), .Q(outLevel[0]), .reset(Reset));  // open: Qn, preset

  assign Z = outLevel[1];

  // Other names for the same wires on the sheet: Clr = Reset; Q0 = outLevel[0]; Q1 = outLevel[1]; J0 = inLevel;
  //   K1 = inLevel; X = inLevel
endmodule

module ContadorUnitario_Past (
  input  push,
  input  Reset,
  output GameOver,
  output [6:0] Unidades,
  output [6:0] Decenas
);

  wire not_1_out, not_2_out, not_3_out, t_ff_1_qn, t_ff_2_qn, t_ff_3_qn, t_ff_4_qn, t_ff_5_qn;
  wire [6:0] t_ff_1_q;

  T_Flip_Flop t_ff_1 (.T(1'b1), .clk(push), .Q(t_ff_1_q[0]), .Qn(t_ff_1_qn), .reset(Reset));  // open: preset
  BCD7SEGx2 bcd7segx2_1 (
    .inBCDx2(t_ff_1_q), .Dg(Decenas[6]), .Df(Decenas[5]), .De(Decenas[4]), .Dd(Decenas[3]), .Dc(Decenas[2]),
    .Db(Decenas[1]), .Da(Decenas[0]), .Ug(Unidades[6]), .Uf(Unidades[5]), .Ue(Unidades[4]), .Ud(Unidades[3]),
    .Uc(Unidades[2]), .Ub(Unidades[1]), .Ua(Unidades[0]));
  not not_1 (not_1_out, t_ff_1_q[0]);
  T_Flip_Flop t_ff_2 (.T(1'b1), .clk(t_ff_1_qn), .Q(t_ff_1_q[1]), .Qn(t_ff_2_qn), .reset(Reset));  // open: preset
  T_Flip_Flop t_ff_3 (.T(1'b1), .clk(t_ff_2_qn), .Q(t_ff_1_q[2]), .Qn(t_ff_3_qn), .reset(Reset));  // open: preset
  not not_2 (not_2_out, t_ff_1_q[2]);
  T_Flip_Flop t_ff_4 (.T(1'b1), .clk(t_ff_3_qn), .Q(t_ff_1_q[3]), .Qn(t_ff_4_qn), .reset(Reset));  // open: preset
  T_Flip_Flop t_ff_5 (.T(1'b1), .clk(t_ff_4_qn), .Q(t_ff_1_q[4]), .Qn(t_ff_5_qn), .reset(Reset));  // open: preset
  T_Flip_Flop t_ff_6 (.T(1'b1), .clk(t_ff_5_qn), .Q(t_ff_1_q[5]));  // open: Qn, reset, preset
  not not_3 (not_3_out, t_ff_1_q[4]);
  _7_Segment_Display u_7_segment_display_1 (
    .g(Decenas[6]), .f(Decenas[5]), .a(Decenas[0]), .b(Decenas[1]), .e(Decenas[4]), .d(Decenas[3]),
    .c(Decenas[2]));  // open: dp
  _7_Segment_Display u_7_segment_display_2 (
    .g(Unidades[6]), .f(Unidades[5]), .a(Unidades[0]), .b(Unidades[1]), .e(Unidades[4]), .d(Unidades[3]),
    .c(Unidades[2]));  // open: dp
  and and_1 (GameOver, not_1_out, t_ff_1_q[1], not_2_out, t_ff_1_q[3], not_3_out);

  // Other names for the same wires on the sheet: a = Decenas[0]; b = Decenas[1]; c = Decenas[2]; d = Decenas[3];
  //   e = Decenas[4]; f = Decenas[5]; g = Decenas[6]; Rst = Reset; a1 = Unidades[0]; b1 = Unidades[1];
  //   c1 = Unidades[2]; d1 = Unidades[3]; e1 = Unidades[4]; f1 = Unidades[5]; g1 = Unidades[6]
endmodule

module MoveControl (
  input  Reset,
  input  [1:0] Control_Joystick,
  input  Clk,
  output [15:0] Ctlr
);

  wire [3:0] counter_1_q;

  Counter #(.max('hf), .width(4)) counter_1 (
    .clr(Reset), .up(Control_Joystick[1]), .count(Control_Joystick[0]), .clk(Clk), .Q(counter_1_q));  // open: load, D, carry
  Decoder #(.select(4)) decoder_1 (
    .out0(Ctlr[15]), .out1(Ctlr[14]), .out2(Ctlr[13]), .out3(Ctlr[12]), .out4(Ctlr[11]), .out5(Ctlr[10]),
    .out6(Ctlr[9]), .out7(Ctlr[8]), .out8(Ctlr[7]), .out9(Ctlr[6]), .out10(Ctlr[5]), .out11(Ctlr[4]),
    .out12(Ctlr[3]), .out13(Ctlr[2]), .out14(Ctlr[1]), .out15(Ctlr[0]), .sel(counter_1_q));  // open: en

  // Notes on the sheet:
  //   Control de movimiento del joystick
endmodule
