// Logisim project Practica1v3.circ as structural Verilog: 9 circuits, main circuit main
module main (
  input  in_1,
  input  in_2,
  input  in_3,
  input  in_4,
  input  in_5,
  input  in_6
);

  wire a, a1, a2, a3, b, b1, b2, b3, c, c1, c2, c3, controldemovimiento_1_a, controldemovimiento_1_b,
       controldemovimiento_1_c, controldemovimiento_1_d, controldemovimiento_1_e, controldemovimiento_1_f,
       controldemovimiento_1_x, controldemovimiento_1_y, conversor_1_a, conversor_1_b, conversor_1_c,
       conversor_1_d, conversor_1_e, conversor_1_f, d, d1, d2, d3, e, e1, e2, e3, f, f1, f2, f3, g, g1, g2,
       g3, led_1_go, led_1_le, led_1_ri, led_1_st;

  Conversor conversor_1 (
    .U(in_1), .V(in_2), .W(in_3), .X(in_4), .Y(in_5), .Z(in_6), .A(conversor_1_a), .B(conversor_1_b),
    .C(conversor_1_c), .D(conversor_1_d), .E(conversor_1_e), .F(conversor_1_f));
  ControlDeMovimiento controldemovimiento_1 (
    .in_1(conversor_1_a), .in_2(conversor_1_b), .in_3(conversor_1_c), .in_4(conversor_1_d),
    .in_5(conversor_1_e), .in_6(conversor_1_f), .A(controldemovimiento_1_a), .B(controldemovimiento_1_b),
    .C(controldemovimiento_1_c), .D(controldemovimiento_1_d), .E(controldemovimiento_1_e),
    .F(controldemovimiento_1_f), .X(controldemovimiento_1_x), .Y(controldemovimiento_1_y));
  BCDtoDO7SEG bcdtodo7seg_1 (
    .A(in_1), .B(in_2), .C(in_3), .D(in_4), .E(in_5), .F(in_6), .A1(a2), .B1(b2), .C1(c2), .D1(d2), .E1(e2),
    .F1(f2), .G1(g2), .A2(a3), .B2(b3), .C2(c3), .D2(d3), .E2(e3), .F2(f3), .G2(g3));
  BCDtoDO7SEG bcdtodo7seg_2 (
    .A(controldemovimiento_1_a), .B(controldemovimiento_1_b), .C(controldemovimiento_1_c),
    .D(controldemovimiento_1_d), .E(controldemovimiento_1_e), .F(controldemovimiento_1_f), .A1(a), .B1(b),
    .C1(c), .D1(d), .E1(e), .F1(f), .G1(g), .A2(a1), .B2(b1), .C2(c1), .D2(d1), .E2(e1), .F2(f1), .G2(g1));
  _7_Segment_Display u_7_segment_display_1 (.g(g2), .f(f2), .a(a2), .b(b2), .e(e2), .d(d2), .c(c2));  // open: dp
  LED led_1 (
    .X(controldemovimiento_1_x), .Y(controldemovimiento_1_y), .GO(led_1_go), .RI(led_1_ri), .LE(led_1_le),
    .ST(led_1_st));
  _7_Segment_Display u_7_segment_display_2 (.g(g3), .f(f3), .a(a3), .b(b3), .e(e3), .d(d3), .c(c3));  // open: dp
  _7_Segment_Display u_7_segment_display_3 (.g(g), .f(f), .a(a), .b(b), .e(e), .d(d), .c(c));  // open: dp
  LED_part GO (.in(led_1_go));
  LED_part RIGH (.in(led_1_ri));
  LED_part LEFT (.in(led_1_le));
  _7_Segment_Display u_7_segment_display_4 (.g(g1), .f(f1), .a(a1), .b(b1), .e(e1), .d(d1), .c(c1));  // open: dp
  LED_part STOP (.in(led_1_st));
endmodule

module BCD7SEG (
  input  w,
  input  x,
  input  y,
  input  z,
  output a,
  output b,
  output c,
  output d,
  output e,
  output f,
  output g
);

  wire and_1_out, and_2_out, and_3_out, and_4_out, and_5_out, and_6_out, and_7_out, and_8_out, and_9_out,
       and_10_out, and_11_out, and_12_out, and_13_out, and_14_out, and_15_out, and_16_out, and_17_out,
       and_18_out, and_19_out, and_20_out, and_21_out, and_22_out, and_23_out, and_24_out, and_25_out,
       and_26_out, not_1_out, not_2_out, not_3_out, not_4_out;

  not not_1 (not_1_out, w);
  not not_2 (not_2_out, x);
  not not_3 (not_3_out, y);
  not not_4 (not_4_out, z);
  and and_1 (and_1_out, not_1_out, not_2_out, not_4_out);
  and and_2 (and_2_out, not_1_out, y);
  and and_3 (and_3_out, not_1_out, x, z);
  and and_4 (and_4_out, w, not_2_out, not_3_out);
  and and_5 (and_5_out, not_1_out, not_2_out);
  and and_6 (and_6_out, not_1_out, not_3_out, not_4_out);
  and and_7 (and_7_out, not_2_out, not_3_out);
  and and_8 (and_8_out, not_1_out, y, z);
  and and_9 (and_9_out, not_2_out, not_3_out);
  and and_10 (and_10_out, not_1_out, z);
  and and_11 (and_11_out, not_1_out, x);
  and and_12 (and_12_out, not_2_out, not_3_out, not_4_out);
  and and_13 (and_13_out, not_1_out, not_2_out, y);
  and and_14 (and_14_out, not_1_out, y, not_4_out);
  and and_15 (and_15_out, not_1_out, x, not_3_out, z);
  and and_16 (and_16_out, not_2_out, not_3_out, not_4_out);
  and and_17 (and_17_out, not_1_out, y, not_4_out);
  and and_18 (and_18_out, not_1_out, not_3_out, not_4_out);
  and and_19 (and_19_out, not_1_out, x, not_3_out);
  and and_20 (and_20_out, not_1_out, x, not_4_out);
  and and_21 (and_21_out, w, not_2_out, not_3_out);
  and and_22 (and_22_out, not_1_out, not_2_out, y);
  and and_23 (and_23_out, not_1_out, x, not_3_out);
  and and_24 (and_24_out, not_1_out, x, not_4_out);
  and and_25 (and_25_out, w, not_2_out, not_3_out);
  and and_26 (and_26_out, w, not_2_out, not_4_out);
  or or_1 (a, and_1_out, and_2_out, and_3_out, and_4_out);
  or or_2 (b, and_5_out, and_6_out, and_7_out, and_8_out);
  or or_3 (c, and_9_out, and_10_out, and_11_out);
  or or_4 (d, and_12_out, and_13_out, and_14_out, and_15_out);
  or or_5 (e, and_16_out, and_17_out);
  or or_6 (f, and_18_out, and_19_out, and_20_out, and_21_out);
  or or_7 (g, and_22_out, and_23_out, and_24_out, and_25_out, and_26_out);
endmodule

module BCDtoDO7SEG (
  input  A,
  input  B,
  input  C,
  input  D,
  input  E,
  input  F,
  output A1,
  output B1,
  output C1,
  output D1,
  output E1,
  output F1,
  output G1,
  output A2,
  output B2,
  output C2,
  output D2,
  output E2,
  output F2,
  output G2
);

  wire convertidordoble_1_w, convertidordoble_1_w1, convertidordoble_1_x, convertidordoble_1_x1,
       convertidordoble_1_y, convertidordoble_1_y1, convertidordoble_1_z, convertidordoble_1_z1;

  ConvertidorDoble convertidordoble_1 (
    .A(A), .B(B), .C(C), .D(D), .E(E), .F(F), .W(convertidordoble_1_w), .X(convertidordoble_1_x),
    .Y(convertidordoble_1_y), .Z(convertidordoble_1_z), .W1(convertidordoble_1_w1),
    .X1(convertidordoble_1_x1), .Y1(convertidordoble_1_y1), .Z1(convertidordoble_1_z1));
  BCD7SEG bcd7seg_1 (
    .w(convertidordoble_1_w), .x(convertidordoble_1_x), .y(convertidordoble_1_y), .z(convertidordoble_1_z),
    .a(A1), .b(B1), .c(C1), .d(D1), .e(E1), .f(F1), .g(G1));
  BCD7SEG bcd7seg_2 (
    .w(convertidordoble_1_w1), .x(convertidordoble_1_x1), .y(convertidordoble_1_y1),
    .z(convertidordoble_1_z1), .a(A2), .b(B2), .c(C2), .d(D2), .e(E2), .f(F2), .g(G2));
endmodule

module LED (
  input  X,
  input  Y,
  output GO,
  output RI,
  output LE,
  output ST
);

  wire not_1_out, not_2_out;

  not not_1 (not_1_out, X);
  not not_2 (not_2_out, Y);
  and and_1 (GO, not_1_out, Y);
  and and_2 (RI, not_1_out, not_2_out);
  and and_3 (LE, X, Y);
  and and_4 (ST, X, not_2_out);
endmodule

module ConvertidorDoble (
  input  A,
  input  B,
  input  C,
  input  D,
  input  E,
  input  F,
  output W,
  output X,
  output Y,
  output Z,
  output W1,
  output X1,
  output Y1,
  output Z1
);

  wire and_1_out, and_2_out, and_3_out, and_4_out, and_5_out, and_6_out, and_7_out, and_8_out, and_9_out,
       and_10_out, and_11_out, and_12_out, and_13_out, and_14_out, and_15_out, and_16_out, and_17_out,
       and_18_out, and_19_out, and_20_out, and_21_out, and_22_out, and_23_out, and_24_out, and_25_out,
       and_26_out, and_27_out, and_28_out, and_29_out, and_30_out, and_31_out, and_32_out, and_33_out,
       and_34_out, and_35_out, and_36_out, and_37_out, and_38_out, and_39_out, and_40_out, and_41_out,
       and_42_out, and_43_out, and_44_out, and_45_out, and_46_out, and_47_out, and_48_out, and_49_out,
       and_50_out, and_51_out, and_52_out, and_53_out, and_54_out, and_55_out, and_56_out, and_57_out,
       and_58_out, and_59_out, and_60_out, and_61_out, and_62_out, and_63_out, and_64_out, and_65_out,
       and_66_out, and_67_out, and_68_out, and_69_out, and_70_out, and_71_out, and_72_out, and_73_out,
       and_74_out, and_75_out, and_76_out, and_77_out, and_78_out, and_79_out, not_1_out, not_2_out,
       not_3_out, not_4_out, not_5_out, not_6_out;

  not not_1 (not_1_out, A);
  not not_2 (not_2_out, B);
  not not_3 (not_3_out, C);
  not not_4 (not_4_out, D);
  not not_5 (not_5_out, E);
  not not_6 (not_6_out, F);
  and and_1 (and_1_out, not_1_out, not_3_out, D, E, not_6_out);
  and and_2 (and_2_out, not_1_out, not_2_out, C, D, not_5_out, F);
  and and_3 (and_3_out, B, not_3_out, not_4_out, not_5_out);
  and and_4 (and_4_out, B, not_4_out, not_5_out, F);
  and and_5 (and_5_out, not_1_out, B, C, not_6_out);
  and and_6 (and_6_out, A, not_2_out, not_3_out, E, not_6_out);
  and and_7 (and_7_out, A, not_2_out, C, not_4_out, F);
  and and_8 (and_8_out, A, not_2_out, C, not_4_out, E);
  and and_9 (and_9_out, A, C, D, not_5_out, not_6_out);
  and and_10 (and_10_out, A, C, D, E, F);
  and and_11 (and_11_out, A, B, not_3_out, not_4_out, not_6_out);
  and and_12 (and_12_out, A, B, not_3_out, not_5_out, F);
  and and_13 (and_13_out, A, C, not_4_out, not_5_out, not_6_out);
  and and_14 (and_14_out, A, C, D, not_5_out, F);
  and and_15 (and_15_out, A, C, D, E, not_6_out);
  and and_16 (and_16_out, A, B, not_3_out, E, F);
  and and_17 (and_17_out, A, B, not_3_out, D, not_6_out);
  and and_18 (and_18_out, A, B, C, not_4_out, E);
  and and_19 (and_19_out, not_2_out, not_3_out, D, E, not_6_out);
  and and_20 (and_20_out, not_1_out, C, D, not_5_out, F);
  and and_21 (and_21_out, not_1_out, B, not_5_out);
  and and_22 (and_22_out, B, not_5_out, F);
  and and_23 (and_23_out, not_1_out, B, D);
  and and_24 (and_24_out, not_1_out, B, C);
  and and_25 (and_25_out, B, C, D);
  and and_26 (and_26_out, A, not_2_out, not_3_out);
  and and_27 (and_27_out, A, not_3_out, not_4_out, not_6_out);
  and and_28 (and_28_out, A, not_2_out, not_4_out, F);
  and and_29 (and_29_out, A, not_2_out, not_4_out, E);
  and and_30 (and_30_out, A, not_2_out, E, F);
  and and_31 (and_31_out, A, not_2_out, D, not_5_out, not_6_out);
  and and_32 (and_32_out, not_1_out, not_2_out, C, E);
  and and_33 (and_33_out, not_1_out, not_2_out, C, D, not_6_out);
  and and_34 (and_34_out, not_1_out, C, D, E, F);
  and and_35 (and_35_out, not_1_out, B, not_3_out, not_4_out, E);
  and and_36 (and_36_out, A, not_2_out, not_3_out, not_5_out);
  and and_37 (and_37_out, A, not_3_out, E, F);
  and and_38 (and_38_out, A, B, not_3_out, D, not_6_out);
  and and_39 (and_39_out, A, B, C, not_4_out, not_6_out);
  and and_40 (and_40_out, A, B, C, not_4_out, E);
  and and_41 (and_41_out, not_1_out, not_3_out, D, E, not_6_out);
  and and_42 (and_42_out, not_1_out, C, not_4_out, not_5_out);
  and and_43 (and_43_out, not_1_out, C, not_5_out, F);
  and and_44 (and_44_out, C, not_4_out, not_5_out, F);
  and and_45 (and_45_out, not_1_out, B, not_3_out, not_4_out);
  and and_46 (and_46_out, B, not_3_out, not_4_out, not_5_out);
  and and_47 (and_47_out, not_1_out, B, C, not_6_out);
  and and_48 (and_48_out, A, not_4_out, E, not_6_out);
  and and_49 (and_49_out, A, not_2_out, not_3_out, D, E);
  and and_50 (and_50_out, A, C, E, F);
  and and_51 (and_51_out, A, C, D, not_5_out, not_6_out);
  and and_52 (and_52_out, A, B, not_3_out, not_5_out, F);
  and and_53 (and_53_out, not_2_out, not_3_out, D, not_5_out);
  and and_54 (and_54_out, not_1_out, not_2_out, D, E, F);
  and and_55 (and_55_out, not_2_out, C, D, E, not_6_out);
  and and_56 (and_56_out, not_1_out, B, C, not_4_out, E, F);
  and and_57 (and_57_out, A, not_2_out, not_3_out, not_4_out, E, F);
  and and_58 (and_58_out, A, not_2_out, D, not_5_out, F);
  and and_59 (and_59_out, A, B, not_3_out, D, E);
  and and_60 (and_60_out, A, B, C, not_4_out, not_5_out, not_6_out);
  and and_61 (and_61_out, not_1_out, not_2_out, not_3_out, E);
  and and_62 (and_62_out, not_1_out, not_3_out, D, E);
  and and_63 (and_63_out, not_1_out, not_2_out, C, D, not_5_out);
  and and_64 (and_64_out, C, D, not_5_out, not_6_out);
  and and_65 (and_65_out, B, not_4_out, not_5_out);
  and and_66 (and_66_out, not_1_out, B, C, not_4_out);
  and and_67 (and_67_out, not_1_out, B, C, not_6_out);
  and and_68 (and_68_out, A, not_3_out, not_4_out, not_6_out);
  and and_69 (and_69_out, A, not_3_out, not_5_out);
  and and_70 (and_70_out, A, not_2_out, E, not_6_out);
  and and_71 (and_71_out, A, not_2_out, C, not_4_out, F);
  and and_72 (and_72_out, A, C, D, E);
  and and_73 (and_73_out, not_1_out, not_2_out, not_4_out, F);
  and and_74 (and_74_out, not_2_out, not_3_out, F);
  and and_75 (and_75_out, not_1_out, E, F);
  and and_76 (and_76_out, not_3_out, E, F);
  and and_77 (and_77_out, B, not_4_out, E, F);
  and and_78 (and_78_out, not_1_out, B, D, F);
  and and_79 (and_79_out, A, C, D, not_5_out, F);
  or or_1 (X, and_13_out, and_14_out, and_15_out, and_16_out, and_17_out, and_18_out);
  or or_2 (Z1, and_73_out, and_74_out, and_75_out, and_76_out, and_77_out, and_78_out, and_79_out);
  or or_3 (W, and_1_out, and_2_out, and_3_out, and_4_out, and_5_out, and_6_out, and_7_out, and_8_out, and_9_out, and_10_out, and_11_out, and_12_out);
  or or_4 (Y, and_19_out, and_20_out, and_21_out, and_22_out, and_23_out, and_24_out, and_25_out, and_26_out, and_27_out, and_28_out, and_29_out, and_30_out, and_31_out);
  or or_5 (Z, and_32_out, and_33_out, and_34_out, and_35_out, and_36_out, and_37_out, and_38_out, and_39_out, and_40_out);
  or or_6 (W1, and_41_out, and_42_out, and_43_out, and_44_out, and_45_out, and_46_out, and_47_out, and_48_out, and_49_out, and_50_out, and_51_out, and_52_out);
  or or_7 (X1, and_53_out, and_54_out, and_55_out, and_56_out, and_57_out, and_58_out, and_59_out, and_60_out);
  or or_8 (Y1, and_61_out, and_62_out, and_63_out, and_64_out, and_65_out, and_66_out, and_67_out, and_68_out, and_69_out, and_70_out, and_71_out, and_72_out);
endmodule

module Movimientos (
  input  A,
  input  B,
  input  C,
  input  D,
  input  E,
  input  F,
  output X,
  output Y
);

  wire and_1_out, and_2_out, and_3_out, and_4_out, and_5_out, and_6_out, and_7_out, and_8_out, and_9_out,
       and_10_out, and_11_out, and_12_out, and_13_out, and_14_out, and_15_out, and_16_out, and_17_out,
       and_18_out, and_19_out, and_20_out, not_1_out, not_2_out, not_3_out, not_4_out, not_5_out, not_6_out;

  not not_1 (not_1_out, A);
  not not_2 (not_2_out, B);
  not not_3 (not_3_out, C);
  not not_4 (not_4_out, D);
  not not_5 (not_5_out, E);
  not not_6 (not_6_out, F);
  and and_1 (and_1_out, not_1_out, not_2_out, not_3_out, not_4_out, F);
  and and_2 (and_2_out, not_1_out, not_3_out, not_4_out, not_5_out, F);
  and and_3 (and_3_out, not_2_out, C, D, not_6_out);
  and and_4 (and_4_out, C, D, not_5_out, not_6_out);
  and and_5 (and_5_out, B, C, D, E, F);
  and and_6 (and_6_out, A, not_5_out, not_6_out);
  and and_7 (and_7_out, A, E, F);
  and and_8 (and_8_out, A, C);
  and and_9 (and_9_out, A, B);
  and and_10 (and_10_out, not_1_out, not_2_out, not_3_out);
  and and_11 (and_11_out, not_1_out, not_3_out, not_4_out);
  and and_12 (and_12_out, not_1_out, not_3_out, not_6_out);
  and and_13 (and_13_out, not_2_out, not_3_out, not_6_out);
  and and_14 (and_14_out, not_1_out, not_2_out, not_5_out, F);
  and and_15 (and_15_out, not_2_out, not_3_out, not_4_out, E);
  and and_16 (and_16_out, not_1_out, not_2_out, D, not_6_out);
  and and_17 (and_17_out, not_2_out, not_3_out, D, not_5_out);
  and and_18 (and_18_out, not_1_out, C, D, not_5_out);
  and and_19 (and_19_out, not_1_out, B, not_5_out, not_6_out);
  and and_20 (and_20_out, not_1_out, B, C, E, F);
  or or_1 (X, and_1_out, and_2_out, and_3_out, and_4_out, and_5_out, and_6_out, and_7_out, and_8_out, and_9_out);
  or or_2 (Y, and_10_out, and_11_out, and_12_out, and_13_out, and_14_out, and_15_out, and_16_out, and_17_out, and_18_out, and_19_out, and_20_out);
endmodule

module ControlDeMovimiento (
  input  in_1,
  input  in_2,
  input  in_3,
  input  in_4,
  input  in_5,
  input  in_6,
  output A,
  output B,
  output C,
  output D,
  output E,
  output F,
  output X,
  output Y
);

  PosicionesSalida posicionessalida_1 (
    .U(in_1), .V(in_2), .W(in_3), .X(in_4), .Y(in_5), .Z(in_6), .A(A), .B(B), .C(C), .D(D), .E(E), .F(F));
  Movimientos movimientos_1 (.A(in_1), .B(in_2), .C(in_3), .D(in_4), .E(in_5), .F(in_6), .X(X), .Y(Y));
endmodule

module PosicionesSalida (
  input  U,
  input  V,
  input  W,
  input  X,
  input  Y,
  input  Z,
  output A,
  output B,
  output C,
  output D,
  output E,
  output F
);

  wire and_1_out, and_2_out, and_3_out, and_4_out, and_5_out, and_6_out, and_7_out, and_8_out, and_9_out,
       and_10_out, and_11_out, and_12_out, and_13_out, and_14_out, and_15_out, and_16_out, and_17_out,
       and_18_out, and_19_out, and_20_out, and_21_out, and_22_out, and_23_out, and_24_out, and_25_out,
       and_26_out, and_27_out, and_28_out, and_29_out, and_30_out, and_31_out, and_32_out, and_33_out,
       and_34_out, and_35_out, and_36_out, and_37_out, and_38_out, and_39_out, and_40_out, and_41_out,
       and_42_out, and_43_out, and_44_out, and_45_out, and_46_out, and_47_out, and_48_out, and_49_out,
       and_50_out, and_51_out, and_52_out, and_53_out, and_54_out, and_55_out, and_56_out, and_57_out,
       and_58_out, and_59_out, and_60_out, and_61_out, and_62_out, and_63_out, and_64_out, and_65_out,
       and_66_out, and_67_out, and_68_out, and_69_out, and_70_out, and_71_out, and_72_out, and_73_out,
       and_74_out, and_75_out, and_76_out, and_77_out, and_78_out, and_79_out, and_80_out, and_81_out,
       and_82_out, not_1_out, not_2_out, not_3_out, not_4_out, not_5_out, not_6_out;

  not not_1 (not_1_out, U);
  not not_2 (not_2_out, V);
  not not_3 (not_3_out, W);
  not not_4 (not_4_out, X);
  not not_5 (not_5_out, Y);
  not not_6 (not_6_out, Z);
  and and_1 (and_1_out, not_3_out, X, not_5_out, not_6_out);
  and and_2 (and_2_out, not_1_out, not_2_out, W, not_6_out);
  and and_3 (and_3_out, not_1_out, not_2_out, W, X);
  and and_4 (and_4_out, not_1_out, V, not_3_out, not_5_out);
  and and_5 (and_5_out, not_1_out, V, not_4_out, not_5_out);
  and and_6 (and_6_out, not_1_out, V, not_3_out, Z);
  and and_7 (and_7_out, not_1_out, V, not_4_out, Z);
  and and_8 (and_8_out, U, not_3_out, X, not_5_out);
  and and_9 (and_9_out, U, W, not_4_out, Y, Z);
  and and_10 (and_10_out, U, V, Y);
  and and_11 (and_11_out, U, V, W);
  and and_12 (and_12_out, not_1_out, not_3_out, not_4_out, not_5_out, not_6_out);
  and and_13 (and_13_out, not_1_out, not_3_out, not_4_out, Y, Z);
  and and_14 (and_14_out, not_1_out, not_2_out, X, not_5_out, Z);
  and and_15 (and_15_out, not_1_out, not_2_out, W, not_5_out, Z);
  and and_16 (and_16_out, not_2_out, W, X, not_5_out);
  and and_17 (and_17_out, not_2_out, W, X, Z);
  and and_18 (and_18_out, not_1_out, V, not_5_out, not_6_out);
  and and_19 (and_19_out, V, not_3_out, not_4_out, not_5_out);
  and and_20 (and_20_out, V, not_4_out, not_5_out, Z);
  and and_21 (and_21_out, V, W, X, not_6_out);
  and and_22 (and_22_out, U, not_2_out, not_4_out, Y, not_6_out);
  and and_23 (and_23_out, U, W, X);
  and and_24 (and_24_out, U, V, W, Y);
  and and_25 (and_25_out, not_1_out, not_2_out, not_3_out, not_5_out, Z);
  and and_26 (and_26_out, not_1_out, not_2_out, not_3_out, not_4_out, Y);
  and and_27 (and_27_out, not_2_out, not_3_out, Y, not_6_out);
  and and_28 (and_28_out, not_1_out, not_2_out, W, not_4_out, not_6_out);
  and and_29 (and_29_out, not_1_out, not_2_out, W, not_5_out, not_6_out);
  and and_30 (and_30_out, W, X, Y, Z);
  and and_31 (and_31_out, V, not_3_out, not_4_out, not_5_out);
  and and_32 (and_32_out, not_1_out, V, W, not_5_out, Z);
  and and_33 (and_33_out, U, not_2_out, not_4_out, not_5_out, Z);
  and and_34 (and_34_out, U, not_3_out, X, not_6_out);
  and and_35 (and_35_out, U, X, Y);
  and and_36 (and_36_out, U, W, X, Z);
  and and_37 (and_37_out, U, V, not_4_out, not_5_out, not_6_out);
  and and_38 (and_38_out, U, V, X, Z);
  and and_39 (and_39_out, not_4_out, not_5_out, not_6_out);
  and and_40 (and_40_out, not_1_out, not_3_out, not_4_out, Y, Z);
  and and_41 (and_41_out, not_1_out, not_3_out, X, not_6_out);
  and and_42 (and_42_out, not_1_out, W, not_4_out, not_6_out);
  and and_43 (and_43_out, not_2_out, W, not_4_out, not_5_out);
  and and_44 (and_44_out, V, not_3_out, not_4_out, not_5_out);
  and and_45 (and_45_out, V, not_3_out, Y, Z);
  and and_46 (and_46_out, not_1_out, V, W, not_4_out, Y);
  and and_47 (and_47_out, not_1_out, V, W, X, not_5_out, Z);
  and and_48 (and_48_out, V, W, X, Y, not_6_out);
  and and_49 (and_49_out, U, not_2_out, not_3_out, not_4_out, not_6_out);
  and and_50 (and_50_out, U, not_2_out, not_4_out, not_5_out);
  and and_51 (and_51_out, U, W, not_5_out, not_6_out);
  and and_52 (and_52_out, U, V, W, X, Y);
  and and_53 (and_53_out, not_1_out, not_2_out, not_3_out, not_4_out, not_6_out);
  and and_54 (and_54_out, not_2_out, not_3_out, not_5_out, Z);
  and and_55 (and_55_out, not_1_out, W, not_4_out, Y);
  and and_56 (and_56_out, not_1_out, not_2_out, W, X, Z);
  and and_57 (and_57_out, not_2_out, W, X, Y, Z);
  and and_58 (and_58_out, not_1_out, V, not_4_out, Z);
  and and_59 (and_59_out, not_1_out, V, W, not_5_out);
  and and_60 (and_60_out, U, not_3_out, not_5_out, Z);
  and and_61 (and_61_out, U, not_3_out, not_4_out, Y);
  and and_62 (and_62_out, U, not_2_out, W, not_5_out, not_6_out);
  and and_63 (and_63_out, U, W, not_4_out, not_5_out, not_6_out);
  and and_64 (and_64_out, U, V, not_3_out, Y, not_6_out);
  and and_65 (and_65_out, U, V, W, Y, Z);
  and and_66 (and_66_out, not_1_out, not_2_out, not_3_out, not_5_out);
  and and_67 (and_67_out, not_1_out, not_2_out, not_4_out, not_5_out);
  and and_68 (and_68_out, not_1_out, not_3_out, not_4_out, not_5_out, not_6_out);
  and and_69 (and_69_out, not_1_out, not_2_out, not_4_out, Z);
  and and_70 (and_70_out, not_1_out, not_2_out, not_5_out, Z);
  and and_71 (and_71_out, not_2_out, not_3_out, not_5_out, Z);
  and and_72 (and_72_out, not_1_out, W, not_4_out, Z);
  and and_73 (and_73_out, not_2_out, W, not_4_out, Z);
  and and_74 (and_74_out, not_2_out, W, X, Y, not_6_out);
  and and_75 (and_75_out, not_1_out, V, not_3_out, Y, not_6_out);
  and and_76 (and_76_out, not_1_out, V, not_4_out, Y);
  and and_77 (and_77_out, V, W, X, not_5_out, not_6_out);
  and and_78 (and_78_out, U, not_2_out, not_3_out, Y, not_6_out);
  and and_79 (and_79_out, U, not_2_out, not_3_out, X, Y);
  and and_80 (and_80_out, U, V, not_3_out, X, not_6_out);
  and and_81 (and_81_out, U, V, W, not_4_out, not_6_out);
  and and_82 (and_82_out, U, V, W, X, Z);
  or or_1 (A, and_1_out, and_2_out, and_3_out, and_4_out, and_5_out, and_6_out, and_7_out, and_8_out, and_9_out, and_10_out, and_11_out);
  or or_2 (B, and_12_out, and_13_out, and_14_out, and_15_out, and_16_out, and_17_out, and_18_out, and_19_out, and_20_out, and_21_out, and_22_out, and_23_out, and_24_out);
  or or_3 (C, and_25_out, and_26_out, and_27_out, and_28_out, and_29_out, and_30_out, and_31_out, and_32_out, and_33_out, and_34_out, and_35_out, and_36_out, and_37_out, and_38_out);
  or or_4 (D, and_39_out, and_40_out, and_41_out, and_42_out, and_43_out, and_44_out, and_45_out, and_46_out, and_47_out, and_48_out, and_49_out, and_50_out, and_51_out, and_52_out);
  or or_5 (E, and_53_out, and_54_out, and_55_out, and_56_out, and_57_out, and_58_out, and_59_out, and_60_out, and_61_out, and_62_out, and_63_out, and_64_out, and_65_out);
  or or_6 (F, and_66_out, and_67_out, and_68_out, and_69_out, and_70_out, and_71_out, and_72_out, and_73_out, and_74_out, and_75_out, and_76_out, and_77_out, and_78_out, and_79_out, and_80_out, and_81_out, and_82_out);
endmodule

module Conversor (
  input  U,
  input  V,
  input  W,
  input  X,
  input  Y,
  input  Z,
  output A,
  output B,
  output C,
  output D,
  output E,
  output F
);

  wire and_1_out, and_2_out, and_3_out, and_4_out, and_5_out, and_6_out, and_7_out, and_8_out, and_9_out,
       and_10_out, and_11_out, and_12_out, and_13_out, and_14_out, and_15_out, and_16_out, and_17_out,
       and_18_out, and_19_out, and_20_out, and_21_out, and_22_out, and_23_out, and_24_out, and_25_out,
       and_26_out, and_27_out, and_28_out, and_29_out, and_30_out, and_31_out, and_32_out, and_33_out,
       and_34_out, and_35_out, and_36_out, and_37_out, and_38_out, and_39_out, and_40_out, and_41_out,
       and_42_out, and_43_out, and_44_out, and_45_out, and_46_out, and_47_out, and_48_out, and_49_out,
       and_50_out, and_51_out, and_52_out, and_53_out, and_54_out, and_55_out, and_56_out, and_57_out,
       and_58_out, and_59_out, and_60_out, and_61_out, and_62_out, and_63_out, and_64_out, and_65_out,
       and_66_out, and_67_out, and_68_out, and_69_out, and_70_out, and_71_out, and_72_out, and_73_out,
       and_74_out, and_75_out, and_76_out, and_77_out, and_78_out, and_79_out, and_80_out, not_1_out,
       not_2_out, not_3_out, not_4_out, not_5_out, not_6_out;

  not not_1 (not_1_out, U);
  not not_2 (not_2_out, V);
  not not_3 (not_3_out, W);
  not not_4 (not_4_out, X);
  not not_5 (not_5_out, Y);
  not not_6 (not_6_out, Z);
  and and_1 (and_1_out, not_2_out, not_3_out, Y, not_6_out);
  and and_2 (and_2_out, not_1_out, not_2_out, not_3_out, X, not_6_out);
  and and_3 (and_3_out, not_1_out, not_3_out, X, Y, not_6_out);
  and and_4 (and_4_out, not_2_out, W, not_4_out, not_5_out);
  and and_5 (and_5_out, not_1_out, not_2_out, W, not_5_out, Z);
  and and_6 (and_6_out, W, X, Y, Z);
  and and_7 (and_7_out, V, not_3_out, not_4_out, not_5_out);
  and and_8 (and_8_out, V, not_4_out, not_5_out, Z);
  and and_9 (and_9_out, not_1_out, V, W, not_6_out);
  and and_10 (and_10_out, U, not_2_out, not_4_out, Y);
  and and_11 (and_11_out, U, W, X, not_5_out, not_6_out);
  and and_12 (and_12_out, U, V, not_3_out, not_4_out, not_6_out);
  and and_13 (and_13_out, U, V, not_3_out, not_5_out, Z);
  and and_14 (and_14_out, not_1_out, not_2_out, not_3_out, not_5_out, Z);
  and and_15 (and_15_out, not_1_out, not_2_out, X, not_5_out, Z);
  and and_16 (and_16_out, not_1_out, not_2_out, X, Y, not_6_out);
  and and_17 (and_17_out, not_2_out, not_3_out, X, Y);
  and and_18 (and_18_out, not_1_out, V, not_4_out, not_5_out);
  and and_19 (and_19_out, not_1_out, V, not_3_out, not_4_out, Z);
  and and_20 (and_20_out, V, not_4_out, not_5_out, Z);
  and and_21 (and_21_out, V, not_3_out, X, not_6_out);
  and and_22 (and_22_out, V, W, not_4_out, Y, not_6_out);
  and and_23 (and_23_out, U, not_3_out, not_5_out, not_6_out);
  and and_24 (and_24_out, U, V, not_3_out, not_6_out);
  and and_25 (and_25_out, U, V, X);
  and and_26 (and_26_out, U, V, W, Y);
  and and_27 (and_27_out, not_1_out, not_3_out, not_4_out, not_5_out, not_6_out);
  and and_28 (and_28_out, not_1_out, not_3_out, not_4_out, Y, Z);
  and and_29 (and_29_out, not_2_out, not_3_out, X, Y);
  and and_30 (and_30_out, not_2_out, X, Y, not_6_out);
  and and_31 (and_31_out, not_1_out, V, not_3_out, not_5_out);
  and and_32 (and_32_out, V, not_3_out, not_4_out, Y, Z);
  and and_33 (and_33_out, not_1_out, V, W, Y, not_6_out);
  and and_34 (and_34_out, V, W, X, not_5_out, not_6_out);
  and and_35 (and_35_out, U, not_2_out, not_4_out, not_5_out, Z);
  and and_36 (and_36_out, U, not_2_out, Y, not_6_out);
  and and_37 (and_37_out, U, not_2_out, X, not_6_out);
  and and_38 (and_38_out, U, not_3_out, X, Y, not_6_out);
  and and_39 (and_39_out, U, W, Y, Z);
  and and_40 (and_40_out, U, not_2_out, W, X);
  and and_41 (and_41_out, U, V, W, not_4_out, not_5_out);
  and and_42 (and_42_out, not_1_out, not_2_out, not_3_out, Y, not_6_out);
  and and_43 (and_43_out, not_3_out, not_4_out, Y, Z);
  and and_44 (and_44_out, not_1_out, not_2_out, X, not_5_out, Z);
  and and_45 (and_45_out, not_2_out, not_3_out, X, Y, not_6_out);
  and and_46 (and_46_out, not_1_out, W, not_5_out, Z);
  and and_47 (and_47_out, not_1_out, W, X, not_6_out);
  and and_48 (and_48_out, V, X, not_5_out, not_6_out);
  and and_49 (and_49_out, not_1_out, V, W, not_5_out);
  and and_50 (and_50_out, not_1_out, V, W, not_4_out, Z);
  and and_51 (and_51_out, U, not_2_out, not_4_out, not_5_out, not_6_out);
  and and_52 (and_52_out, U, not_2_out, not_3_out, Z);
  and and_53 (and_53_out, U, not_3_out, X, Z);
  and and_54 (and_54_out, U, X, Y, Z);
  and and_55 (and_55_out, U, W, not_5_out, not_6_out);
  and and_56 (and_56_out, not_1_out, not_3_out, not_5_out, Z);
  and and_57 (and_57_out, not_1_out, not_4_out, not_5_out, Z);
  and and_58 (and_58_out, not_1_out, not_2_out, not_3_out, X, Z);
  and and_59 (and_59_out, not_2_out, W, Y);
  and and_60 (and_60_out, W, Y, Z);
  and and_61 (and_61_out, not_1_out, W, X, not_5_out, not_6_out);
  and and_62 (and_62_out, not_1_out, V, not_4_out, not_5_out);
  and and_63 (and_63_out, not_1_out, V, not_3_out, X, not_6_out);
  and and_64 (and_64_out, U, not_2_out, not_3_out, not_4_out, not_5_out);
  and and_65 (and_65_out, U, not_4_out, Y, Z);
  and and_66 (and_66_out, U, not_2_out, X, Y, not_6_out);
  and and_67 (and_67_out, U, W, X, Y);
  and and_68 (and_68_out, U, V, not_3_out, not_4_out, Y);
  and and_69 (and_69_out, not_4_out, not_5_out, Z);
  and and_70 (and_70_out, not_1_out, not_2_out, not_3_out, X);
  and and_71 (and_71_out, not_1_out, not_2_out, X, not_5_out, not_6_out);
  and and_72 (and_72_out, not_1_out, not_2_out, W, not_4_out, Y, not_6_out);
  and and_73 (and_73_out, not_1_out, V, not_3_out, not_4_out, Z);
  and and_74 (and_74_out, V, not_3_out, X, not_6_out);
  and and_75 (and_75_out, not_1_out, V, X, Y);
  and and_76 (and_76_out, U, not_5_out, Z);
  and and_77 (and_77_out, U, W, not_4_out, not_5_out);
  and and_78 (and_78_out, U, not_2_out, W, Z);
  and and_79 (and_79_out, U, W, X, Z);
  and and_80 (and_80_out, U, not_2_out, W, X, Y);
  or or_1 (A, and_1_out, and_2_out, and_3_out, and_4_out, and_5_out, and_6_out, and_7_out, and_8_out, and_9_out, and_10_out, and_11_out, and_12_out, and_13_out);
  or or_2 (B, and_14_out, and_15_out, and_16_out, and_17_out, and_18_out, and_19_out, and_20_out, and_21_out, and_22_out, and_23_out, and_24_out, and_25_out, and_26_out);
  or or_3 (C, and_27_out, and_28_out, and_29_out, and_30_out, and_31_out, and_32_out, and_33_out, and_34_out, and_35_out, and_36_out, and_37_out, and_38_out, and_39_out, and_40_out, and_41_out);
  or or_4 (D, and_42_out, and_43_out, and_44_out, and_45_out, and_46_out, and_47_out, and_48_out, and_49_out, and_50_out, and_51_out, and_52_out, and_53_out, and_54_out, and_55_out);
  or or_5 (E, and_56_out, and_57_out, and_58_out, and_59_out, and_60_out, and_61_out, and_62_out, and_63_out, and_64_out, and_65_out, and_66_out, and_67_out, and_68_out);
  or or_6 (F, and_69_out, and_70_out, and_71_out, and_72_out, and_73_out, and_74_out, and_75_out, and_76_out, and_77_out, and_78_out, and_79_out, and_80_out);
endmodule
