// Logisim project Practica1.circ as structural Verilog: 2 circuits, main circuit main
module main (
  input  in_1,
  input  in_2,
  input  in_3,
  input  in_4
);

  wire decoder7seg_1_a1, decoder7seg_1_b1, decoder7seg_1_c1, decoder7seg_1_d1, decoder7seg_1_e1,
       decoder7seg_1_f1, decoder7seg_1_g1;

  decoder7seg decoder7seg_1 (
    .W(in_1), .X(in_2), .Y(in_3), .Z(in_4), .a1(decoder7seg_1_a1), .b1(decoder7seg_1_b1),
    .c1(decoder7seg_1_c1), .d1(decoder7seg_1_d1), .e1(decoder7seg_1_e1), .f1(decoder7seg_1_f1),
    .g1(decoder7seg_1_g1));
  _7_Segment_Display u_7_segment_display_1 (
    .g(decoder7seg_1_g1), .f(decoder7seg_1_f1), .a(decoder7seg_1_a1), .b(decoder7seg_1_b1),
    .e(decoder7seg_1_e1), .d(decoder7seg_1_d1), .c(decoder7seg_1_c1));  // open: dp
endmodule

module decoder7seg (
  input  W,
  input  X,
  input  Y,
  input  Z,
  output a1,
  output b1,
  output c1,
  output d1,
  output e1,
  output f1,
  output g1
);

  wire and_1_out, and_2_out, and_3_out, and_4_out, and_5_out, and_6_out, and_7_out, and_8_out, and_9_out,
       and_10_out, and_11_out, and_12_out, and_13_out, and_14_out, and_15_out, and_16_out, and_17_out,
       and_18_out, and_19_out, and_20_out, and_21_out, and_22_out, and_23_out, and_24_out, and_25_out,
       not_1_out, not_2_out, not_3_out, not_4_out;

  not not_1 (not_1_out, W);
  not not_2 (not_2_out, X);
  not not_3 (not_3_out, Y);
  not not_4 (not_4_out, Z);
  and and_1 (and_1_out, not_2_out, not_3_out, not_4_out);
  and and_2 (and_2_out, not_1_out, X, Z);
  and and_3 (and_3_out, not_1_out, Y);
  and and_4 (and_4_out, W, not_2_out, not_3_out);
  and and_5 (and_5_out, not_2_out, not_3_out);
  and and_6 (and_6_out, not_1_out, not_2_out);
  and and_7 (and_7_out, not_1_out, not_3_out, not_4_out);
  and and_8 (and_8_out, not_1_out, Y, Z);
  and and_9 (and_9_out, not_2_out, not_3_out);
  and and_10 (and_10_out, not_1_out, X);
  and and_11 (and_11_out, not_1_out, Z);
  and and_12 (and_12_out, not_2_out, not_3_out, not_4_out);
  and and_13 (and_13_out, not_1_out, not_2_out, Y);
  and and_14 (and_14_out, not_1_out, Y, not_4_out);
  and and_15 (and_15_out, not_1_out, X, not_3_out, Z);
  and and_16 (and_16_out, not_2_out, not_3_out, not_4_out);
  and and_17 (and_17_out, not_1_out, Y, not_4_out);
  and and_18 (and_18_out, not_2_out, not_3_out, not_4_out);
  and and_19 (and_19_out, not_1_out, X, not_4_out);
  and and_20 (and_20_out, not_1_out, X, not_3_out);
  and and_21 (and_21_out, W, not_2_out, not_3_out);
  and and_22 (and_22_out, not_1_out, X, not_3_out);
  and and_23 (and_23_out, W, not_2_out, not_3_out);
  and and_24 (and_24_out, not_1_out, not_2_out, Y);
  and and_25 (and_25_out, not_1_out, Y, not_4_out);
  or A (a1, and_1_out, and_2_out, and_3_out, and_4_out);
  or B (b1, and_5_out, and_6_out, and_7_out, and_8_out);
  or C (c1, and_9_out, and_10_out, and_11_out);
  or D (d1, and_12_out, and_13_out, and_14_out, and_15_out);
  or E (e1, and_16_out, and_17_out);
  or F (f1, and_18_out, and_19_out, and_20_out, and_21_out);
  or G (g1, and_22_out, and_23_out, and_24_out, and_25_out);
endmodule
