// Logisim project Practica1.circ as structural Verilog: 10 circuits, main circuit main
module main (
  input  in_1,
  input  in_2,
  input  in_3,
  input  in_4,
  input  in_5,
  input  in_6
);

  wire a, a1, a2, a3, b, b1, b2, b3, c, c1, c2, c3, d, d1, d2, d3, e, e1, e2, e3, f, f1, f2, f3, g, g1, g2,
       g3, led_1_go, led_1_le, led_1_ri, led_1_st, movementocontrol_1_a, movementocontrol_1_b,
       movementocontrol_1_c, movementocontrol_1_d, movementocontrol_1_e, movementocontrol_1_f,
       movementocontrol_1_x, movementocontrol_1_y, movimientosdeentrada_1_u, movimientosdeentrada_1_v,
       movimientosdeentrada_1_w, movimientosdeentrada_1_x, movimientosdeentrada_1_y, movimientosdeentrada_1_z;

  MovimientosDeEntrada movimientosdeentrada_1 (
    .A(in_1), .B(in_2), .C(in_3), .D(in_4), .E(in_5), .F(in_6), .U(movimientosdeentrada_1_u),
    .V(movimientosdeentrada_1_v), .W(movimientosdeentrada_1_w), .X(movimientosdeentrada_1_x),
    .Y(movimientosdeentrada_1_y), .Z(movimientosdeentrada_1_z));
  BCDtoDO7SEG bcdtodo7seg_1 (
    .A(movimientosdeentrada_1_u), .B(movimientosdeentrada_1_v), .C(movimientosdeentrada_1_w),
    .D(movimientosdeentrada_1_x), .E(movimientosdeentrada_1_y), .F(movimientosdeentrada_1_z), .A1(a2),
    .B1(b2), .C1(c2), .D1(d2), .E1(e2), .F1(f2), .G1(g2), .A2(a3), .B2(b3), .C2(c3), .D2(d3), .E2(e3),
    .F2(f3), .G2(g3));
  MovementoControl movementocontrol_1 (
    .in_1(in_1), .in_2(in_2), .in_3(in_3), .in_4(in_4), .in_5(in_5), .in_6(in_6), .A(movementocontrol_1_a),
    .B(movementocontrol_1_b), .C(movementocontrol_1_c), .D(movementocontrol_1_d), .E(movementocontrol_1_e),
    .F(movementocontrol_1_f), .X(movementocontrol_1_x), .Y(movementocontrol_1_y));
  BCDtoDO7SEG bcdtodo7seg_2 (
    .A(movementocontrol_1_a), .B(movementocontrol_1_b), .C(movementocontrol_1_c), .D(movementocontrol_1_d),
    .E(movementocontrol_1_e), .F(movementocontrol_1_f), .A1(a), .B1(b), .C1(c), .D1(d), .E1(e), .F1(f),
    .G1(g), .A2(a1), .B2(b1), .C2(c1), .D2(d1), .E2(e1), .F2(f1), .G2(g1));
  _7_Segment_Display u_7_segment_display_1 (.g(g2), .f(f2), .a(a2), .b(b2), .e(e2), .d(d2), .c(c2));  // open: dp
  _7_Segment_Display u_7_segment_display_2 (.g(g3), .f(f3), .a(a3), .b(b3), .e(e3), .d(d3), .c(c3));  // open: dp
  _7_Segment_Display u_7_segment_display_3 (.g(g), .f(f), .a(a), .b(b), .e(e), .d(d), .c(c));  // open: dp
  _7_Segment_Display u_7_segment_display_4 (.g(g1), .f(f1), .a(a1), .b(b1), .e(e1), .d(d1), .c(c1));  // open: dp
  LED led_1 (
    .X(movementocontrol_1_x), .Y(movementocontrol_1_y), .GO(led_1_go), .RI(led_1_ri), .LE(led_1_le),
    .ST(led_1_st));
  LED_part GO (.in(led_1_go));
  LED_part RIGH (.in(led_1_ri));
  LED_part LEFT (.in(led_1_le));
  LED_part STOP (.in(led_1_st));
endmodule

module BCD7SEG (
  input  w,
  input  x,
  input  y,
  input  z,
  output a,
  output b,
  output c,
  output d,
  output e,
  output f,
  output g
);

  wire and_1_out, and_2_out, and_3_out, and_4_out, and_5_out, and_6_out, and_7_out, and_8_out, and_9_out,
       and_10_out, and_11_out, and_12_out, and_13_out, and_14_out, and_15_out, and_16_out, and_17_out,
       and_18_out, and_19_out, and_20_out, and_21_out, and_22_out, and_23_out, and_24_out, and_25_out,
       not_1_out, not_2_out, not_3_out, not_4_out;

  not not_1 (not_1_out, w);
  not not_2 (not_2_out, x);
  not not_3 (not_3_out, y);
  not not_4 (not_4_out, z);
  and and_1 (and_1_out, not_1_out, not_2_out, not_4_out);
  and and_2 (and_2_out, not_1_out, y);
  and and_3 (and_3_out, not_1_out, x, z);
  and and_4 (and_4_out, w, not_2_out, not_3_out);
  and and_5 (and_5_out, not_1_out, not_2_out);
  and and_6 (and_6_out, not_1_out, not_3_out, not_4_out);
  and and_7 (and_7_out, not_2_out, not_3_out);
  and and_8 (and_8_out, not_1_out, y, z);
  and and_9 (and_9_out, not_2_out, not_3_out);
  and and_10 (and_10_out, not_1_out, z);
  and and_11 (and_11_out, not_1_out, x);
  and and_12 (and_12_out, not_2_out, not_3_out, not_4_out);
  and and_13 (and_13_out, not_1_out, not_2_out, y);
  and and_14 (and_14_out, not_1_out, y, not_4_out);
  and and_15 (and_15_out, not_1_out, x, not_3_out, z);
  and and_16 (and_16_out, not_2_out, not_3_out, not_4_out);
  and and_17 (and_17_out, not_1_out, y, not_4_out);
  and and_18 (and_18_out, not_1_out, not_3_out, not_4_out);
  and and_19 (and_19_out, not_1_out, x, not_3_out);
  and and_20 (and_20_out, not_1_out, x, not_4_out);
  and and_21 (and_21_out, w, not_2_out, not_3_out);
  and and_22 (and_22_out, not_1_out, not_2_out, y);
  and and_23 (and_23_out, not_1_out, x, not_3_out);
  and and_24 (and_24_out, not_1_out, x, not_4_out);
  and and_25 (and_25_out, w, not_2_out, not_3_out);
  or or_1 (a, and_1_out, and_2_out, and_3_out, and_4_out);
  or or_2 (b, and_5_out, and_6_out, and_7_out, and_8_out);
  or or_3 (c, and_9_out, and_10_out, and_11_out);
  or or_4 (d, and_12_out, and_13_out, and_14_out, and_15_out);
  or or_5 (e, and_16_out, and_17_out);
  or or_6 (f, and_18_out, and_19_out, and_20_out, and_21_out);
  or or_7 (g, and_22_out, and_23_out, and_24_out, and_25_out);
endmodule

module BCDtoDO7SEG (
  input  A,
  input  B,
  input  C,
  input  D,
  input  E,
  input  F,
  output A1,
  output B1,
  output C1,
  output D1,
  output E1,
  output F1,
  output G1,
  output A2,
  output B2,
  output C2,
  output D2,
  output E2,
  output F2,
  output G2
);

  wire convertidordoble_1_w, convertidordoble_1_w1, convertidordoble_1_x, convertidordoble_1_x1,
       convertidordoble_1_y, convertidordoble_1_y1, convertidordoble_1_z, convertidordoble_1_z1;

  ConvertidorDoble convertidordoble_1 (
    .A(A), .B(B), .C(C), .D(D), .E(E), .F(F), .W(convertidordoble_1_w), .X(convertidordoble_1_x),
    .Y(convertidordoble_1_y), .Z(convertidordoble_1_z), .W1(convertidordoble_1_w1),
    .X1(convertidordoble_1_x1), .Y1(convertidordoble_1_y1), .Z1(convertidordoble_1_z1));
  BCD7SEG bcd7seg_1 (
    .w(convertidordoble_1_w), .x(convertidordoble_1_x), .y(convertidordoble_1_y), .z(convertidordoble_1_z),
    .a(A1), .b(B1), .c(C1), .d(D1), .e(E1), .f(F1), .g(G1));
  BCD7SEG bcd7seg_2 (
    .w(convertidordoble_1_w1), .x(convertidordoble_1_x1), .y(convertidordoble_1_y1),
    .z(convertidordoble_1_z1), .a(A2), .b(B2), .c(C2), .d(D2), .e(E2), .f(F2), .g(G2));
endmodule

module LED (
  input  X,
  input  Y,
  output GO,
  output RI,
  output LE,
  output ST
);

  wire not_1_out, not_2_out;

  not not_1 (not_1_out, X);
  not not_2 (not_2_out, Y);
  and and_1 (GO, not_1_out, Y);
  and and_2 (RI, not_1_out, not_2_out);
  and and_3 (LE, X, Y);
  and and_4 (ST, X, not_2_out);
endmodule

module PosicionInicial (
  input  in_1,
  input  in_2,
  input  in_3,
  input  in_4,
  input  in_5,
  input  in_6,
  output U,
  output V,
  output W,
  output X,
  output Y,
  output Z
);

  MovimientosDeEntrada movimientosdeentrada_1 (
    .A(in_1), .B(in_2), .C(in_3), .D(in_4), .E(in_5), .F(in_6), .U(U), .V(V), .W(W), .X(X), .Y(Y), .Z(Z));
endmodule

module ConvertidorDoble (
  input  A,
  input  B,
  input  C,
  input  D,
  input  E,
  input  F,
  output W,
  output X,
  output Y,
  output Z,
  output W1,
  output X1,
  output Y1,
  output Z1
);

  wire and_1_out, and_2_out, and_3_out, and_4_out, and_5_out, and_6_out, and_7_out, and_8_out, and_9_out,
       and_10_out, and_11_out, and_12_out, and_13_out, and_14_out, and_15_out, and_16_out, and_17_out,
       and_18_out, and_19_out, and_20_out, and_21_out, and_22_out, and_23_out, and_24_out, and_25_out,
       and_26_out, and_27_out, and_28_out, and_29_out, and_30_out, and_31_out, and_32_out, and_33_out,
       and_34_out, and_35_out, and_36_out, and_37_out, and_38_out, not_1_out, not_2_out, not_3_out,
       not_4_out, not_5_out;

  not not_1 (not_1_out, A);
  not not_2 (not_2_out, B);
  not not_3 (not_3_out, C);
  not not_4 (not_4_out, D);
  not not_5 (not_5_out, E);
  and and_1 (and_1_out, A, C);
  and and_2 (and_2_out, A, B);
  and and_3 (and_3_out, not_1_out, B, D);
  and and_4 (and_4_out, not_1_out, B, C);
  and and_5 (and_5_out, B, C, D);
  and and_6 (and_6_out, A, not_2_out, not_3_out);
  and and_7 (and_7_out, not_1_out, not_2_out, C, E);
  and and_8 (and_8_out, not_1_out, not_2_out, C, D);
  and and_9 (and_9_out, not_1_out, C, D, E);
  and and_10 (and_10_out, not_1_out, B, not_3_out, not_4_out);
  and and_11 (and_11_out, A, not_2_out, not_3_out);
  and and_12 (and_12_out, A, not_3_out, E);
  and and_13 (and_13_out, A, not_3_out, D);
  and and_14 (and_14_out, A, B, C, not_4_out);
  and and_15 (and_15_out, not_1_out, not_2_out, C, not_4_out, not_5_out);
  and and_16 (and_16_out, not_1_out, B, not_3_out, not_4_out, E);
  and and_17 (and_17_out, not_1_out, B, C, D, not_5_out);
  and and_18 (and_18_out, A, not_2_out, not_3_out, D, E);
  and and_19 (and_19_out, A, B, not_3_out, not_4_out, not_5_out);
  and and_20 (and_20_out, A, B, C, not_4_out, E);
  and and_21 (and_21_out, not_2_out, not_3_out, D, not_5_out);
  and and_22 (and_22_out, not_1_out, not_2_out, D, E);
  and and_23 (and_23_out, not_1_out, B, not_4_out, not_5_out);
  and and_24 (and_24_out, not_1_out, B, C, not_4_out);
  and and_25 (and_25_out, B, C, not_4_out, not_5_out);
  and and_26 (and_26_out, A, not_2_out, not_3_out, not_4_out, E);
  and and_27 (and_27_out, A, not_2_out, C, D);
  and and_28 (and_28_out, A, B, not_3_out, D, E);
  and and_29 (and_29_out, not_1_out, not_2_out, not_3_out, E);
  and and_30 (and_30_out, not_1_out, not_3_out, D, E);
  and and_31 (and_31_out, not_1_out, not_2_out, C, D, not_5_out);
  and and_32 (and_32_out, not_1_out, B, not_3_out, not_4_out, not_5_out);
  and and_33 (and_33_out, not_1_out, B, C, not_4_out, E);
  and and_34 (and_34_out, A, not_2_out, not_3_out, not_5_out);
  and and_35 (and_35_out, A, not_3_out, D, not_5_out);
  and and_36 (and_36_out, A, not_2_out, C, E);
  and and_37 (and_37_out, A, C, D, E);
  and and_38 (and_38_out, A, B, C, not_4_out, not_5_out);
  or or_1 (X, and_1_out, and_2_out);
  or or_2 (Y, and_3_out, and_4_out, and_5_out, and_6_out);
  or or_3 (W1, and_15_out, and_16_out, and_17_out, and_18_out, and_19_out, and_20_out);
  or or_4 (Z, and_7_out, and_8_out, and_9_out, and_10_out, and_11_out, and_12_out, and_13_out, and_14_out);
  or or_5 (X1, and_21_out, and_22_out, and_23_out, and_24_out, and_25_out, and_26_out, and_27_out, and_28_out);
  or or_6 (Y1, and_29_out, and_30_out, and_31_out, and_32_out, and_33_out, and_34_out, and_35_out, and_36_out, and_37_out, and_38_out);

  assign W = 1'b0;
  assign Z1 = F;
endmodule

module Movimientos (
  input  A,
  input  B,
  input  C,
  input  D,
  input  E,
  input  F,
  output X,
  output Y
);

  wire and_1_out, and_2_out, and_3_out, and_4_out, and_5_out, and_6_out, and_7_out, and_8_out, and_9_out,
       and_10_out, and_11_out, and_12_out, and_13_out, and_14_out, and_15_out, and_16_out, and_17_out,
       and_18_out, not_1_out, not_2_out, not_3_out, not_4_out, not_5_out, not_6_out;

  not not_1 (not_1_out, A);
  not not_2 (not_2_out, B);
  not not_3 (not_3_out, C);
  not not_4 (not_4_out, D);
  not not_5 (not_5_out, E);
  not not_6 (not_6_out, F);
  and and_1 (and_1_out, not_1_out, not_2_out, not_3_out, not_4_out, F);
  and and_2 (and_2_out, not_1_out, not_3_out, not_4_out, not_5_out, F);
  and and_3 (and_3_out, not_1_out, not_2_out, C, D, not_6_out);
  and and_4 (and_4_out, not_1_out, C, D, not_5_out, not_6_out);
  and and_5 (and_5_out, not_1_out, B, C, D, E, F);
  and and_6 (and_6_out, A, not_2_out, not_3_out, not_5_out, not_6_out);
  and and_7 (and_7_out, A, not_2_out, not_3_out, E, F);
  and and_8 (and_8_out, not_1_out, not_2_out, not_3_out);
  and and_9 (and_9_out, not_1_out, not_3_out, not_4_out);
  and and_10 (and_10_out, not_1_out, not_3_out, not_6_out);
  and and_11 (and_11_out, not_2_out, not_3_out, not_6_out);
  and and_12 (and_12_out, not_1_out, not_2_out, not_5_out, F);
  and and_13 (and_13_out, not_2_out, not_3_out, not_4_out, E);
  and and_14 (and_14_out, not_1_out, not_2_out, D, not_6_out);
  and and_15 (and_15_out, not_2_out, not_3_out, D, not_5_out);
  and and_16 (and_16_out, not_1_out, C, D, not_5_out);
  and and_17 (and_17_out, not_1_out, B, not_5_out, not_6_out);
  and and_18 (and_18_out, not_1_out, B, C, E, F);
  or or_1 (X, and_1_out, and_2_out, and_3_out, and_4_out, and_5_out, and_6_out, and_7_out);
  or or_2 (Y, and_8_out, and_9_out, and_10_out, and_11_out, and_12_out, and_13_out, and_14_out, and_15_out, and_16_out, and_17_out, and_18_out);
endmodule

module MovimientosDeEntrada (
  input  A,
  input  B,
  input  C,
  input  D,
  input  E,
  input  F,
  output U,
  output V,
  output W,
  output X,
  output Y,
  output Z
);

  wire and_1_out, and_2_out, and_3_out, and_4_out, and_5_out, and_6_out, and_7_out, and_8_out, and_9_out,
       and_10_out, and_11_out, and_12_out, and_13_out, and_14_out, and_15_out, and_16_out, and_17_out,
       and_18_out, and_19_out, and_20_out, and_21_out, and_22_out, and_23_out, and_24_out, and_25_out,
       and_26_out, and_27_out, and_28_out, and_29_out, and_30_out, and_31_out, and_32_out, and_33_out,
       and_34_out, and_35_out, and_36_out, and_37_out, and_38_out, and_39_out, and_40_out, and_41_out,
       and_42_out, and_43_out, and_44_out, and_45_out, and_46_out, and_47_out, and_48_out, and_49_out,
       and_50_out, and_51_out, and_52_out, and_53_out, and_54_out, and_55_out, and_56_out, and_57_out,
       and_58_out, not_1_out, not_2_out, not_3_out, not_4_out, not_5_out, not_6_out;

  not not_1 (not_1_out, A);
  not not_2 (not_2_out, B);
  not not_3 (not_3_out, C);
  not not_4 (not_4_out, D);
  not not_5 (not_5_out, E);
  not not_6 (not_6_out, F);
  and and_1 (and_1_out, not_2_out, not_3_out, D, not_5_out, F);
  and and_2 (and_2_out, not_1_out, not_2_out, C, F);
  and and_3 (and_3_out, not_1_out, not_2_out, C, D, E);
  and and_4 (and_4_out, not_1_out, B, not_3_out, not_5_out);
  and and_5 (and_5_out, not_1_out, B, not_3_out, not_6_out);
  and and_6 (and_6_out, not_1_out, B, not_4_out, not_5_out);
  and and_7 (and_7_out, not_1_out, B, not_4_out, not_6_out);
  and and_8 (and_8_out, not_1_out, B, not_5_out, not_6_out);
  and and_9 (and_9_out, A, not_2_out, not_3_out, D, E, not_6_out);
  and and_10 (and_10_out, not_1_out, not_3_out, not_4_out, not_5_out);
  and and_11 (and_11_out, not_1_out, not_3_out, not_5_out, not_6_out);
  and and_12 (and_12_out, not_1_out, not_2_out, not_3_out, D, not_6_out);
  and and_13 (and_13_out, not_1_out, not_2_out, C, E, not_6_out);
  and and_14 (and_14_out, not_1_out, C, D, not_5_out, F);
  and and_15 (and_15_out, not_1_out, B, not_5_out, F);
  and and_16 (and_16_out, not_1_out, B, not_4_out, E, not_6_out);
  and and_17 (and_17_out, not_1_out, B, C, D, F);
  and and_18 (and_18_out, A, not_2_out, not_3_out, not_4_out, E, F);
  and and_19 (and_19_out, not_1_out, not_2_out, not_3_out, E);
  and and_20 (and_20_out, not_2_out, not_3_out, not_4_out, E);
  and and_21 (and_21_out, not_1_out, not_2_out, not_3_out, D, not_6_out);
  and and_22 (and_22_out, not_1_out, not_2_out, C, not_4_out, F);
  and and_23 (and_23_out, not_1_out, not_2_out, C, not_5_out, F);
  and and_24 (and_24_out, not_1_out, B, not_3_out, not_4_out, not_5_out);
  and and_25 (and_25_out, not_1_out, B, not_3_out, not_4_out, not_6_out);
  and and_26 (and_26_out, not_1_out, B, C, E, not_6_out);
  and and_27 (and_27_out, A, not_2_out, not_3_out, not_4_out, not_6_out);
  and and_28 (and_28_out, A, not_2_out, not_3_out, D, F);
  and and_29 (and_29_out, not_1_out, not_4_out, not_5_out, F);
  and and_30 (and_30_out, not_2_out, not_3_out, not_4_out, not_5_out, F);
  and and_31 (and_31_out, not_1_out, not_3_out, D, not_5_out);
  and and_32 (and_32_out, not_1_out, not_3_out, D, F);
  and and_33 (and_33_out, not_1_out, not_2_out, C, not_4_out, E);
  and and_34 (and_34_out, not_1_out, B, not_3_out, not_4_out, E, not_6_out);
  and and_35 (and_35_out, not_1_out, B, C, not_4_out, not_5_out);
  and and_36 (and_36_out, not_1_out, B, C, E, F);
  and and_37 (and_37_out, not_1_out, B, C, D, not_6_out);
  and and_38 (and_38_out, A, not_2_out, not_3_out, not_4_out, E);
  and and_39 (and_39_out, not_1_out, not_2_out, not_3_out, not_4_out);
  and and_40 (and_40_out, not_1_out, not_3_out, not_4_out, not_6_out);
  and and_41 (and_41_out, not_2_out, not_3_out, not_4_out, E);
  and and_42 (and_42_out, not_2_out, not_3_out, E, not_6_out);
  and and_43 (and_43_out, not_1_out, not_2_out, not_4_out, E, F);
  and and_44 (and_44_out, not_1_out, C, D, not_6_out);
  and and_45 (and_45_out, not_1_out, B, not_3_out, not_5_out, not_6_out);
  and and_46 (and_46_out, not_1_out, B, C, not_4_out, E);
  and and_47 (and_47_out, not_1_out, B, C, D, not_5_out);
  and and_48 (and_48_out, A, not_2_out, not_3_out, D, not_6_out);
  and and_49 (and_49_out, not_1_out, not_2_out, not_4_out, not_5_out, F);
  and and_50 (and_50_out, not_1_out, not_3_out, not_4_out, not_5_out, F);
  and and_51 (and_51_out, not_1_out, not_2_out, E, not_6_out);
  and and_52 (and_52_out, not_1_out, not_2_out, not_3_out, D, not_5_out);
  and and_53 (and_53_out, not_1_out, D, not_5_out, not_6_out);
  and and_54 (and_54_out, not_1_out, not_2_out, C, D, E);
  and and_55 (and_55_out, not_1_out, B, not_3_out, E, F);
  and and_56 (and_56_out, not_1_out, B, C, not_4_out, E);
  and and_57 (and_57_out, not_1_out, B, C, D, not_5_out);
  and and_58 (and_58_out, A, not_2_out, not_3_out, E);
  or or_1 (U, and_1_out, and_2_out, and_3_out, and_4_out, and_5_out, and_6_out, and_7_out, and_8_out, and_9_out);
  or or_2 (V, and_10_out, and_11_out, and_12_out, and_13_out, and_14_out, and_15_out, and_16_out, and_17_out, and_18_out);
  or or_3 (W, and_19_out, and_20_out, and_21_out, and_22_out, and_23_out, and_24_out, and_25_out, and_26_out, and_27_out, and_28_out);
  or or_4 (X, and_29_out, and_30_out, and_31_out, and_32_out, and_33_out, and_34_out, and_35_out, and_36_out, and_37_out, and_38_out);
  or or_5 (Y, and_39_out, and_40_out, and_41_out, and_42_out, and_43_out, and_44_out, and_45_out, and_46_out, and_47_out, and_48_out);
  or or_6 (Z, and_49_out, and_50_out, and_51_out, and_52_out, and_53_out, and_54_out, and_55_out, and_56_out, and_57_out, and_58_out);
endmodule

module MovimientosDeSalida (
  input  A,
  input  B,
  input  C,
  input  D,
  input  E,
  input  F,
  output U,
  output V,
  output W,
  output X,
  output Y,
  output Z
);

  wire and_1_out, and_2_out, and_3_out, and_4_out, and_5_out, and_6_out, and_7_out, and_8_out, and_9_out,
       and_10_out, and_11_out, and_12_out, and_13_out, and_14_out, and_15_out, and_16_out, and_17_out,
       and_18_out, and_19_out, and_20_out, and_21_out, and_22_out, and_23_out, and_24_out, and_25_out,
       and_26_out, and_27_out, and_28_out, and_29_out, and_30_out, and_31_out, and_32_out, and_33_out,
       and_34_out, and_35_out, and_36_out, and_37_out, and_38_out, and_39_out, and_40_out, and_41_out,
       and_42_out, and_43_out, and_44_out, and_45_out, and_46_out, and_47_out, and_48_out, and_49_out,
       and_50_out, and_51_out, and_52_out, and_53_out, and_54_out, and_55_out, and_56_out, and_57_out,
       and_58_out, and_59_out, and_60_out, and_61_out, not_1_out, not_2_out, not_3_out, not_4_out, not_5_out,
       not_6_out;

  not not_1 (not_1_out, A);
  not not_2 (not_2_out, B);
  not not_3 (not_3_out, C);
  not not_4 (not_4_out, D);
  not not_5 (not_5_out, E);
  not not_6 (not_6_out, F);
  and and_1 (and_1_out, not_2_out, not_3_out, D, not_5_out, not_6_out);
  and and_2 (and_2_out, not_1_out, not_2_out, C, not_6_out);
  and and_3 (and_3_out, not_1_out, not_2_out, C, D);
  and and_4 (and_4_out, not_1_out, B, not_3_out, not_5_out);
  and and_5 (and_5_out, not_1_out, B, not_4_out, not_5_out);
  and and_6 (and_6_out, not_1_out, B, not_3_out, F);
  and and_7 (and_7_out, not_1_out, B, not_4_out, F);
  and and_8 (and_8_out, A, not_2_out, not_3_out, D, not_5_out);
  and and_9 (and_9_out, not_1_out, not_3_out, not_4_out, not_5_out, not_6_out);
  and and_10 (and_10_out, not_1_out, not_3_out, not_4_out, E, F);
  and and_11 (and_11_out, not_1_out, not_2_out, D, not_5_out, F);
  and and_12 (and_12_out, not_1_out, not_2_out, C, not_5_out, F);
  and and_13 (and_13_out, not_1_out, not_2_out, C, D, not_5_out);
  and and_14 (and_14_out, not_1_out, not_2_out, C, D, F);
  and and_15 (and_15_out, not_1_out, B, not_4_out, not_5_out);
  and and_16 (and_16_out, not_1_out, B, not_5_out, not_6_out);
  and and_17 (and_17_out, not_1_out, B, C, D, not_6_out);
  and and_18 (and_18_out, A, not_2_out, not_3_out, not_4_out, E, not_6_out);
  and and_19 (and_19_out, not_1_out, not_2_out, not_3_out, not_5_out, F);
  and and_20 (and_20_out, not_2_out, not_3_out, not_4_out, not_5_out, F);
  and and_21 (and_21_out, not_1_out, not_2_out, not_3_out, not_4_out, E);
  and and_22 (and_22_out, not_2_out, not_3_out, E, not_6_out);
  and and_23 (and_23_out, not_1_out, not_2_out, C, not_4_out, not_6_out);
  and and_24 (and_24_out, not_1_out, not_2_out, C, not_5_out, not_6_out);
  and and_25 (and_25_out, not_1_out, C, D, E, F);
  and and_26 (and_26_out, not_1_out, B, not_3_out, not_4_out, not_5_out);
  and and_27 (and_27_out, not_1_out, B, C, not_5_out, F);
  and and_28 (and_28_out, A, not_2_out, not_3_out, D, not_6_out);
  and and_29 (and_29_out, A, not_2_out, not_3_out, D, E);
  and and_30 (and_30_out, not_1_out, not_3_out, not_5_out, not_6_out);
  and and_31 (and_31_out, not_1_out, not_3_out, not_4_out, E, F);
  and and_32 (and_32_out, not_1_out, not_3_out, D, not_6_out);
  and and_33 (and_33_out, not_1_out, not_2_out, C, not_4_out, not_5_out);
  and and_34 (and_34_out, not_1_out, C, not_4_out, not_6_out);
  and and_35 (and_35_out, not_1_out, B, not_3_out, not_4_out, not_5_out);
  and and_36 (and_36_out, not_1_out, B, not_3_out, D, E);
  and and_37 (and_37_out, not_1_out, B, C, not_4_out, E);
  and and_38 (and_38_out, not_1_out, B, C, E, not_6_out);
  and and_39 (and_39_out, not_1_out, B, C, D, not_5_out, F);
  and and_40 (and_40_out, A, not_2_out, not_3_out, not_4_out, not_5_out);
  and and_41 (and_41_out, A, not_2_out, not_3_out, not_4_out, not_6_out);
  and and_42 (and_42_out, not_1_out, not_2_out, not_3_out, not_4_out, not_6_out);
  and and_43 (and_43_out, not_2_out, not_3_out, not_5_out, F);
  and and_44 (and_44_out, not_1_out, C, not_4_out, E);
  and and_45 (and_45_out, not_1_out, not_2_out, C, D, F);
  and and_46 (and_46_out, not_1_out, B, not_4_out, F);
  and and_47 (and_47_out, not_1_out, B, C, D, not_5_out);
  and and_48 (and_48_out, A, not_2_out, not_3_out, not_4_out, E);
  and and_49 (and_49_out, not_1_out, not_2_out, not_3_out, not_5_out);
  and and_50 (and_50_out, not_1_out, not_2_out, not_4_out, not_5_out);
  and and_51 (and_51_out, not_1_out, not_3_out, not_4_out, not_5_out, not_6_out);
  and and_52 (and_52_out, not_1_out, not_2_out, not_4_out, F);
  and and_53 (and_53_out, not_1_out, not_2_out, not_5_out, F);
  and and_54 (and_54_out, not_2_out, not_3_out, not_5_out, F);
  and and_55 (and_55_out, not_1_out, C, not_4_out, F);
  and and_56 (and_56_out, not_1_out, not_2_out, C, D, E, not_6_out);
  and and_57 (and_57_out, not_1_out, B, not_3_out, E, not_6_out);
  and and_58 (and_58_out, not_1_out, B, not_4_out, E);
  and and_59 (and_59_out, not_1_out, B, C, D, not_5_out, not_6_out);
  and and_60 (and_60_out, A, not_2_out, not_3_out, E, not_6_out);
  and and_61 (and_61_out, A, not_2_out, not_3_out, D, E);
  or or_1 (Y, and_42_out, and_43_out, and_44_out, and_45_out, and_46_out, and_47_out, and_48_out);
  or or_2 (U, and_1_out, and_2_out, and_3_out, and_4_out, and_5_out, and_6_out, and_7_out, and_8_out);
  or or_3 (V, and_9_out, and_10_out, and_11_out, and_12_out, and_13_out, and_14_out, and_15_out, and_16_out, and_17_out, and_18_out);
  or or_4 (W, and_19_out, and_20_out, and_21_out, and_22_out, and_23_out, and_24_out, and_25_out, and_26_out, and_27_out, and_28_out, and_29_out);
  or or_5 (X, and_30_out, and_31_out, and_32_out, and_33_out, and_34_out, and_35_out, and_36_out, and_37_out, and_38_out, and_39_out, and_40_out, and_41_out);
  or or_6 (Z, and_49_out, and_50_out, and_51_out, and_52_out, and_53_out, and_54_out, and_55_out, and_56_out, and_57_out, and_58_out, and_59_out, and_60_out, and_61_out);
endmodule

module MovementoControl (
  input  in_1,
  input  in_2,
  input  in_3,
  input  in_4,
  input  in_5,
  input  in_6,
  output A,
  output B,
  output C,
  output D,
  output E,
  output F,
  output X,
  output Y
);

  MovimientosDeSalida movimientosdesalida_1 (
    .A(in_1), .B(in_2), .C(in_3), .D(in_4), .E(in_5), .F(in_6), .U(A), .V(B), .W(C), .X(D), .Y(E), .Z(F));
  Movimientos movimientos_1 (.A(in_1), .B(in_2), .C(in_3), .D(in_4), .E(in_5), .F(in_6), .X(X), .Y(Y));
endmodule
