// Logisim project Practica1v2.circ as structural Verilog: 10 circuits, main circuit main
module main (
  input  [5:0] in_1
);

  wire a, a1, a2, a3, b, b1, b2, b3, c, c1, c2, c3, controldemovimiento_1_x, controldemovimiento_1_y,
       conversor_1_a, conversor_1_b, conversor_1_c, conversor_1_d, conversor_1_e, conversor_1_f, d, d1, d2,
       d3, e, e1, e2, e3, f, f1, f2, f3, g, g1, g2, g3, led_1_go, led_1_le, led_1_ri, led_1_st;
  wire [5:0] controldemovimiento_1_a, posicionesentrada_1_a;

  Conversor conversor_1 (
    .U(in_1[0]), .V(in_1[1]), .W(in_1[2]), .X(in_1[3]), .Y(in_1[4]), .Z(in_1[5]), .A(conversor_1_a),
    .B(conversor_1_b), .C(conversor_1_c), .D(conversor_1_d), .E(conversor_1_e), .F(conversor_1_f));
  PosicionesEntrada posicionesentrada_1 (
    .U(conversor_1_a), .V(conversor_1_b), .W(conversor_1_c), .X(conversor_1_d), .Y(conversor_1_e),
    .Z(conversor_1_f), .A(posicionesentrada_1_a[0]), .B(posicionesentrada_1_a[1]),
    .C(posicionesentrada_1_a[2]), .D(posicionesentrada_1_a[3]), .E(posicionesentrada_1_a[4]),
    .F(posicionesentrada_1_a[5]));
  ControlDeMovimiento controldemovimiento_1 (
    .in_1(conversor_1_a), .in_2(conversor_1_b), .in_3(conversor_1_c), .in_4(conversor_1_d),
    .in_5(conversor_1_e), .in_6(conversor_1_f), .A(controldemovimiento_1_a[0]),
    .B(controldemovimiento_1_a[1]), .C(controldemovimiento_1_a[2]), .D(controldemovimiento_1_a[3]),
    .E(controldemovimiento_1_a[4]), .F(controldemovimiento_1_a[5]), .X(controldemovimiento_1_x),
    .Y(controldemovimiento_1_y));
  BCDtoDO7SEG bcdtodo7seg_1 (
    .A(posicionesentrada_1_a), .out_2({a2, b2, c2, d2, e2, f2, g2}), .out_3({a3, b3, c3, d3, e3, f3, g3}));
  BCDtoDO7SEG bcdtodo7seg_2 (
    .A(controldemovimiento_1_a), .out_2({a, b, c, d, e, f, g}), .out_3({a1, b1, c1, d1, e1, f1, g1}));
  _7_Segment_Display u_7_segment_display_1 (.g(g2), .f(f2), .a(a2), .b(b2), .e(e2), .d(d2), .c(c2));  // open: dp
  _7_Segment_Display u_7_segment_display_2 (.g(g3), .f(f3), .a(a3), .b(b3), .e(e3), .d(d3), .c(c3));  // open: dp
  LED_part GO (.in(led_1_go));
  LED led_1 (
    .X(controldemovimiento_1_x), .Y(controldemovimiento_1_y), .GO(led_1_go), .RI(led_1_ri), .LE(led_1_le),
    .ST(led_1_st));
  _7_Segment_Display u_7_segment_display_3 (.g(g), .f(f), .a(a), .b(b), .e(e), .d(d), .c(c));  // open: dp
  LED_part RIGH (.in(led_1_ri));
  LED_part LEFT (.in(led_1_le));
  LED_part STOP (.in(led_1_st));
  _7_Segment_Display u_7_segment_display_4 (.g(g1), .f(f1), .a(a1), .b(b1), .e(e1), .d(d1), .c(c1));  // open: dp
endmodule

module BCD7SEG (
  input  [3:0] in_1,
  output [6:0] out_2
);

  wire and_1_out, and_2_out, and_3_out, and_4_out, and_5_out, and_6_out, and_7_out, and_8_out, and_9_out,
       and_10_out, and_11_out, and_12_out, and_13_out, and_14_out, and_15_out, and_16_out, and_17_out,
       and_18_out, and_19_out, and_20_out, and_21_out, and_22_out, and_23_out, and_24_out, and_25_out,
       not_1_out, not_2_out, not_3_out, not_4_out;

  not not_1 (not_1_out, in_1[0]);
  not not_2 (not_2_out, in_1[1]);
  not not_3 (not_3_out, in_1[2]);
  not not_4 (not_4_out, in_1[3]);
  and and_1 (and_1_out, not_1_out, not_2_out, not_4_out);
  and and_2 (and_2_out, not_1_out, in_1[2]);
  and and_3 (and_3_out, not_1_out, in_1[1], in_1[3]);
  and and_4 (and_4_out, in_1[0], not_2_out, not_3_out);
  and and_5 (and_5_out, not_1_out, not_2_out);
  and and_6 (and_6_out, not_1_out, not_3_out, not_4_out);
  and and_7 (and_7_out, not_2_out, not_3_out);
  and and_8 (and_8_out, not_1_out, in_1[2], in_1[3]);
  and and_9 (and_9_out, not_2_out, not_3_out);
  and and_10 (and_10_out, not_1_out, in_1[3]);
  and and_11 (and_11_out, not_1_out, in_1[1]);
  and and_12 (and_12_out, not_2_out, not_3_out, not_4_out);
  and and_13 (and_13_out, not_1_out, not_2_out, in_1[2]);
  and and_14 (and_14_out, not_1_out, in_1[2], not_4_out);
  and and_15 (and_15_out, not_1_out, in_1[1], not_3_out, in_1[3]);
  and and_16 (and_16_out, not_2_out, not_3_out, not_4_out);
  and and_17 (and_17_out, not_1_out, in_1[2], not_4_out);
  and and_18 (and_18_out, not_1_out, not_3_out, not_4_out);
  and and_19 (and_19_out, not_1_out, in_1[1], not_3_out);
  and and_20 (and_20_out, not_1_out, in_1[1], not_4_out);
  and and_21 (and_21_out, in_1[0], not_2_out, not_3_out);
  and and_22 (and_22_out, not_1_out, not_2_out, in_1[2]);
  and and_23 (and_23_out, not_1_out, in_1[1], not_3_out);
  and and_24 (and_24_out, not_1_out, in_1[1], not_4_out);
  and and_25 (and_25_out, in_1[0], not_2_out, not_3_out);
  or or_1 (out_2[0], and_1_out, and_2_out, and_3_out, and_4_out);
  or or_2 (out_2[1], and_5_out, and_6_out, and_7_out, and_8_out);
  or or_3 (out_2[2], and_9_out, and_10_out, and_11_out);
  or or_4 (out_2[3], and_12_out, and_13_out, and_14_out, and_15_out);
  or or_5 (out_2[4], and_16_out, and_17_out);
  or or_6 (out_2[5], and_18_out, and_19_out, and_20_out, and_21_out);
  or or_7 (out_2[6], and_22_out, and_23_out, and_24_out, and_25_out);
endmodule

module BCDtoDO7SEG (
  input  [5:0] A,
  output [6:0] out_2,
  output [6:0] out_3
);

  wire [3:0] convertidordoble_1_w, convertidordoble_1_w1;

  ConvertidorDoble convertidordoble_1 (
    .in_1(A), .W(convertidordoble_1_w[0]), .X(convertidordoble_1_w[1]), .Y(convertidordoble_1_w[2]),
    .Z(convertidordoble_1_w[3]), .W1(convertidordoble_1_w1[0]), .X1(convertidordoble_1_w1[1]),
    .Y1(convertidordoble_1_w1[2]), .Z1(convertidordoble_1_w1[3]));
  BCD7SEG bcd7seg_1 (.in_1(convertidordoble_1_w), .out_2(out_2));
  BCD7SEG bcd7seg_2 (.in_1(convertidordoble_1_w1), .out_2(out_3));
endmodule

module LED (
  input  X,
  input  Y,
  output GO,
  output RI,
  output LE,
  output ST
);

  wire not_1_out, not_2_out;

  not not_1 (not_1_out, X);
  not not_2 (not_2_out, Y);
  and and_1 (GO, not_1_out, Y);
  and and_2 (RI, not_1_out, not_2_out);
  and and_3 (LE, X, Y);
  and and_4 (ST, X, not_2_out);
endmodule

module ConvertidorDoble (
  input  [5:0] in_1,
  output W,
  output X,
  output Y,
  output Z,
  output W1,
  output X1,
  output Y1,
  output Z1
);

  wire [5:4] divider_1_out, divider_1_rem;

  Divider #(.width(6)) divider_1 (
    .a(in_1), .b(6'b001010), .out({divider_1_out, Z, Y, X, W}), .rem({divider_1_rem, Z1, Y1, X1, W1}));  // open: upper
endmodule

module Movimientos (
  input  A,
  input  B,
  input  C,
  input  D,
  input  E,
  input  F,
  output X,
  output Y
);

  wire and_1_out, and_2_out, and_3_out, and_4_out, and_5_out, and_6_out, and_7_out, and_8_out, and_9_out,
       and_10_out, and_11_out, and_12_out, and_13_out, and_14_out, and_15_out, and_16_out, and_17_out,
       and_18_out, not_1_out, not_2_out, not_3_out, not_4_out, not_5_out, not_6_out;

  not not_1 (not_1_out, A);
  not not_2 (not_2_out, B);
  not not_3 (not_3_out, C);
  not not_4 (not_4_out, D);
  not not_5 (not_5_out, E);
  not not_6 (not_6_out, F);
  and and_1 (and_1_out, not_1_out, not_2_out, not_3_out, not_4_out, F);
  and and_2 (and_2_out, not_1_out, not_3_out, not_4_out, not_5_out, F);
  and and_3 (and_3_out, not_1_out, not_2_out, C, D, not_6_out);
  and and_4 (and_4_out, not_1_out, C, D, not_5_out, not_6_out);
  and and_5 (and_5_out, not_1_out, B, C, D, E, F);
  and and_6 (and_6_out, A, not_2_out, not_3_out, not_5_out, not_6_out);
  and and_7 (and_7_out, A, not_2_out, not_3_out, E, F);
  and and_8 (and_8_out, not_1_out, not_2_out, not_3_out);
  and and_9 (and_9_out, not_1_out, not_3_out, not_4_out);
  and and_10 (and_10_out, not_1_out, not_3_out, not_6_out);
  and and_11 (and_11_out, not_2_out, not_3_out, not_6_out);
  and and_12 (and_12_out, not_1_out, not_2_out, not_5_out, F);
  and and_13 (and_13_out, not_2_out, not_3_out, not_4_out, E);
  and and_14 (and_14_out, not_1_out, not_2_out, D, not_6_out);
  and and_15 (and_15_out, not_2_out, not_3_out, D, not_5_out);
  and and_16 (and_16_out, not_1_out, C, D, not_5_out);
  and and_17 (and_17_out, not_1_out, B, not_5_out, not_6_out);
  and and_18 (and_18_out, not_1_out, B, C, E, F);
  or or_1 (X, and_1_out, and_2_out, and_3_out, and_4_out, and_5_out, and_6_out, and_7_out);
  or or_2 (Y, and_8_out, and_9_out, and_10_out, and_11_out, and_12_out, and_13_out, and_14_out, and_15_out, and_16_out, and_17_out, and_18_out);
endmodule

module ControlDeMovimiento (
  input  in_1,
  input  in_2,
  input  in_3,
  input  in_4,
  input  in_5,
  input  in_6,
  output A,
  output B,
  output C,
  output D,
  output E,
  output F,
  output X,
  output Y
);

  PosicionesSalida posicionessalida_1 (
    .U(in_1), .V(in_2), .W(in_3), .X(in_4), .Y(in_5), .Z(in_6), .A(A), .B(B), .C(C), .D(D), .E(E), .F(F));
  Movimientos movimientos_1 (.A(in_1), .B(in_2), .C(in_3), .D(in_4), .E(in_5), .F(in_6), .X(X), .Y(Y));
endmodule

module PosicionesSalida (
  input  U,
  input  V,
  input  W,
  input  X,
  input  Y,
  input  Z,
  output A,
  output B,
  output C,
  output D,
  output E,
  output F
);

  wire and_1_out, and_2_out, and_3_out, and_4_out, and_5_out, and_6_out, and_7_out, and_8_out, and_9_out,
       and_10_out, and_11_out, and_12_out, and_13_out, and_14_out, and_15_out, and_16_out, and_17_out,
       and_18_out, and_19_out, and_20_out, and_21_out, and_22_out, and_23_out, and_24_out, and_25_out,
       and_26_out, and_27_out, and_28_out, and_29_out, and_30_out, and_31_out, and_32_out, and_33_out,
       and_34_out, and_35_out, and_36_out, and_37_out, and_38_out, and_39_out, and_40_out, and_41_out,
       and_42_out, and_43_out, and_44_out, and_45_out, and_46_out, and_47_out, and_48_out, and_49_out,
       and_50_out, and_51_out, and_52_out, and_53_out, and_54_out, and_55_out, and_56_out, and_57_out,
       and_58_out, and_59_out, and_60_out, and_61_out, not_1_out, not_2_out, not_3_out, not_4_out, not_5_out,
       not_6_out;

  not not_1 (not_1_out, U);
  not not_2 (not_2_out, V);
  not not_3 (not_3_out, W);
  not not_4 (not_4_out, X);
  not not_5 (not_5_out, Y);
  not not_6 (not_6_out, Z);
  and and_1 (and_1_out, not_2_out, not_3_out, X, not_5_out, not_6_out);
  and and_2 (and_2_out, not_1_out, not_2_out, W, not_6_out);
  and and_3 (and_3_out, not_1_out, not_2_out, W, X);
  and and_4 (and_4_out, not_1_out, V, not_3_out, not_5_out);
  and and_5 (and_5_out, not_1_out, V, not_4_out, not_5_out);
  and and_6 (and_6_out, not_1_out, V, not_3_out, Z);
  and and_7 (and_7_out, not_1_out, V, not_4_out, Z);
  and and_8 (and_8_out, U, not_2_out, not_3_out, X, not_5_out);
  and and_9 (and_9_out, not_1_out, not_3_out, not_4_out, not_5_out, not_6_out);
  and and_10 (and_10_out, not_1_out, not_3_out, not_4_out, Y, Z);
  and and_11 (and_11_out, not_1_out, not_2_out, X, not_5_out, Z);
  and and_12 (and_12_out, not_1_out, not_2_out, W, not_5_out, Z);
  and and_13 (and_13_out, not_1_out, not_2_out, W, X, not_5_out);
  and and_14 (and_14_out, not_1_out, not_2_out, W, X, Z);
  and and_15 (and_15_out, not_1_out, V, not_4_out, not_5_out);
  and and_16 (and_16_out, not_1_out, V, not_5_out, not_6_out);
  and and_17 (and_17_out, not_1_out, V, W, X, not_6_out);
  and and_18 (and_18_out, U, not_2_out, not_3_out, not_4_out, Y, not_6_out);
  and and_19 (and_19_out, not_1_out, not_2_out, not_3_out, not_5_out, Z);
  and and_20 (and_20_out, not_2_out, not_3_out, not_4_out, not_5_out, Z);
  and and_21 (and_21_out, not_1_out, not_2_out, not_3_out, not_4_out, Y);
  and and_22 (and_22_out, not_2_out, not_3_out, Y, not_6_out);
  and and_23 (and_23_out, not_1_out, not_2_out, W, not_4_out, not_6_out);
  and and_24 (and_24_out, not_1_out, not_2_out, W, not_5_out, not_6_out);
  and and_25 (and_25_out, not_1_out, W, X, Y, Z);
  and and_26 (and_26_out, not_1_out, V, not_3_out, not_4_out, not_5_out);
  and and_27 (and_27_out, not_1_out, V, W, not_5_out, Z);
  and and_28 (and_28_out, U, not_2_out, not_3_out, X, not_6_out);
  and and_29 (and_29_out, U, not_2_out, not_3_out, X, Y);
  and and_30 (and_30_out, not_1_out, not_3_out, not_5_out, not_6_out);
  and and_31 (and_31_out, not_1_out, not_3_out, not_4_out, Y, Z);
  and and_32 (and_32_out, not_1_out, not_3_out, X, not_6_out);
  and and_33 (and_33_out, not_1_out, not_2_out, W, not_4_out, not_5_out);
  and and_34 (and_34_out, not_1_out, W, not_4_out, not_6_out);
  and and_35 (and_35_out, not_1_out, V, not_3_out, not_4_out, not_5_out);
  and and_36 (and_36_out, not_1_out, V, not_3_out, X, Y);
  and and_37 (and_37_out, not_1_out, V, W, not_4_out, Y);
  and and_38 (and_38_out, not_1_out, V, W, Y, not_6_out);
  and and_39 (and_39_out, not_1_out, V, W, X, not_5_out, Z);
  and and_40 (and_40_out, U, not_2_out, not_3_out, not_4_out, not_5_out);
  and and_41 (and_41_out, U, not_2_out, not_3_out, not_4_out, not_6_out);
  and and_42 (and_42_out, not_1_out, not_2_out, not_3_out, not_4_out, not_6_out);
  and and_43 (and_43_out, not_2_out, not_3_out, not_5_out, Z);
  and and_44 (and_44_out, not_1_out, W, not_4_out, Y);
  and and_45 (and_45_out, not_1_out, not_2_out, W, X, Z);
  and and_46 (and_46_out, not_1_out, V, not_4_out, Z);
  and and_47 (and_47_out, not_1_out, V, W, not_5_out);
  and and_48 (and_48_out, U, not_2_out, not_3_out, not_4_out, Y);
  and and_49 (and_49_out, not_1_out, not_2_out, not_3_out, not_5_out);
  and and_50 (and_50_out, not_1_out, not_2_out, not_4_out, not_5_out);
  and and_51 (and_51_out, not_1_out, not_3_out, not_4_out, not_5_out, not_6_out);
  and and_52 (and_52_out, not_1_out, not_2_out, not_4_out, Z);
  and and_53 (and_53_out, not_1_out, not_2_out, not_5_out, Z);
  and and_54 (and_54_out, not_2_out, not_3_out, not_5_out, Z);
  and and_55 (and_55_out, not_1_out, W, not_4_out, Z);
  and and_56 (and_56_out, not_1_out, not_2_out, W, X, Y, not_6_out);
  and and_57 (and_57_out, not_1_out, V, not_3_out, Y, not_6_out);
  and and_58 (and_58_out, not_1_out, V, not_4_out, Y);
  and and_59 (and_59_out, not_1_out, V, W, X, not_5_out, not_6_out);
  and and_60 (and_60_out, U, not_2_out, not_3_out, Y, not_6_out);
  and and_61 (and_61_out, U, not_2_out, not_3_out, X, Y);
  or or_1 (E, and_42_out, and_43_out, and_44_out, and_45_out, and_46_out, and_47_out, and_48_out);
  or or_2 (A, and_1_out, and_2_out, and_3_out, and_4_out, and_5_out, and_6_out, and_7_out, and_8_out);
  or or_3 (B, and_9_out, and_10_out, and_11_out, and_12_out, and_13_out, and_14_out, and_15_out, and_16_out, and_17_out, and_18_out);
  or or_4 (C, and_19_out, and_20_out, and_21_out, and_22_out, and_23_out, and_24_out, and_25_out, and_26_out, and_27_out, and_28_out, and_29_out);
  or or_5 (D, and_30_out, and_31_out, and_32_out, and_33_out, and_34_out, and_35_out, and_36_out, and_37_out, and_38_out, and_39_out, and_40_out, and_41_out);
  or or_6 (F, and_49_out, and_50_out, and_51_out, and_52_out, and_53_out, and_54_out, and_55_out, and_56_out, and_57_out, and_58_out, and_59_out, and_60_out, and_61_out);
endmodule

module PosicionesEntrada (
  input  U,
  input  V,
  input  W,
  input  X,
  input  Y,
  input  Z,
  output A,
  output B,
  output C,
  output D,
  output E,
  output F
);

  wire and_1_out, and_2_out, and_3_out, and_4_out, and_5_out, and_6_out, and_7_out, and_8_out, and_9_out,
       and_10_out, and_11_out, and_12_out, and_13_out, and_14_out, and_15_out, and_16_out, and_17_out,
       and_18_out, and_19_out, and_20_out, and_21_out, and_22_out, and_23_out, and_24_out, and_25_out,
       and_26_out, and_27_out, and_28_out, and_29_out, and_30_out, and_31_out, and_32_out, and_33_out,
       and_34_out, and_35_out, and_36_out, and_37_out, and_38_out, and_39_out, and_40_out, and_41_out,
       and_42_out, and_43_out, and_44_out, and_45_out, and_46_out, and_47_out, and_48_out, and_49_out,
       and_50_out, and_51_out, and_52_out, and_53_out, and_54_out, and_55_out, and_56_out, and_57_out,
       not_1_out, not_2_out, not_3_out, not_4_out, not_5_out, not_6_out;

  not not_1 (not_1_out, U);
  not not_2 (not_2_out, V);
  not not_3 (not_3_out, W);
  not not_4 (not_4_out, X);
  not not_5 (not_5_out, Y);
  not not_6 (not_6_out, Z);
  and and_1 (and_1_out, not_2_out, not_3_out, X, not_5_out, Z);
  and and_2 (and_2_out, not_1_out, not_2_out, W, Z);
  and and_3 (and_3_out, not_1_out, not_2_out, W, X, Y);
  and and_4 (and_4_out, not_1_out, V, not_3_out, not_5_out);
  and and_5 (and_5_out, not_1_out, V, not_3_out, not_6_out);
  and and_6 (and_6_out, not_1_out, V, not_4_out, not_5_out);
  and and_7 (and_7_out, not_1_out, V, not_4_out, not_6_out);
  and and_8 (and_8_out, not_1_out, V, not_5_out, not_6_out);
  and and_9 (and_9_out, U, not_2_out, not_3_out, X, Y, not_6_out);
  and and_10 (and_10_out, not_1_out, not_3_out, not_4_out, not_5_out);
  and and_11 (and_11_out, not_1_out, not_3_out, not_5_out, not_6_out);
  and and_12 (and_12_out, not_1_out, not_2_out, not_3_out, X, not_6_out);
  and and_13 (and_13_out, not_1_out, not_2_out, W, Y, not_6_out);
  and and_14 (and_14_out, not_1_out, W, X, not_5_out, Z);
  and and_15 (and_15_out, not_1_out, V, not_5_out, Z);
  and and_16 (and_16_out, not_1_out, V, not_4_out, Y, not_6_out);
  and and_17 (and_17_out, not_1_out, V, W, X, Z);
  and and_18 (and_18_out, U, not_2_out, not_3_out, not_4_out, Y, Z);
  and and_19 (and_19_out, not_1_out, not_2_out, not_3_out, Y);
  and and_20 (and_20_out, not_2_out, not_3_out, not_4_out, Y);
  and and_21 (and_21_out, not_1_out, not_2_out, not_3_out, X, not_6_out);
  and and_22 (and_22_out, not_1_out, not_2_out, W, not_4_out, Z);
  and and_23 (and_23_out, not_1_out, not_2_out, W, not_5_out, Z);
  and and_24 (and_24_out, not_1_out, V, not_3_out, not_4_out, not_5_out);
  and and_25 (and_25_out, not_1_out, V, not_3_out, not_4_out, not_6_out);
  and and_26 (and_26_out, not_1_out, V, W, Y, not_6_out);
  and and_27 (and_27_out, U, not_2_out, not_3_out, not_4_out, not_6_out);
  and and_28 (and_28_out, U, not_2_out, not_3_out, X, Z);
  and and_29 (and_29_out, not_1_out, not_4_out, not_5_out, Z);
  and and_30 (and_30_out, not_2_out, not_3_out, not_4_out, not_5_out, Z);
  and and_31 (and_31_out, not_1_out, not_3_out, X, not_5_out);
  and and_32 (and_32_out, not_1_out, not_3_out, X, Z);
  and and_33 (and_33_out, not_1_out, not_2_out, W, not_4_out, Y);
  and and_34 (and_34_out, not_1_out, V, not_3_out, not_4_out, Y, not_6_out);
  and and_35 (and_35_out, not_1_out, V, W, not_4_out, not_5_out);
  and and_36 (and_36_out, not_1_out, V, W, Y, Z);
  and and_37 (and_37_out, not_1_out, V, W, X, not_6_out);
  and and_38 (and_38_out, U, not_2_out, not_3_out, not_4_out, Y);
  and and_39 (and_39_out, not_1_out, not_2_out, not_3_out, not_4_out);
  and and_40 (and_40_out, not_2_out, not_3_out, not_4_out, Y);
  and and_41 (and_41_out, not_2_out, not_3_out, Y, not_6_out);
  and and_42 (and_42_out, not_1_out, W, not_4_out, Y, Z);
  and and_43 (and_43_out, not_1_out, W, X, not_6_out);
  and and_44 (and_44_out, not_1_out, V, not_3_out, not_5_out, not_6_out);
  and and_45 (and_45_out, not_1_out, V, not_4_out, Y, not_6_out);
  and and_46 (and_46_out, not_1_out, V, W, not_5_out, Z);
  and and_47 (and_47_out, U, not_2_out, not_3_out, X, not_6_out);
  and and_48 (and_48_out, not_1_out, not_2_out, not_4_out, not_5_out, Z);
  and and_49 (and_49_out, not_1_out, not_3_out, not_4_out, not_5_out, Z);
  and and_50 (and_50_out, not_1_out, not_2_out, Y, not_6_out);
  and and_51 (and_51_out, not_1_out, not_2_out, not_3_out, X, not_5_out);
  and and_52 (and_52_out, not_1_out, X, not_5_out, not_6_out);
  and and_53 (and_53_out, not_1_out, not_2_out, W, X, Y);
  and and_54 (and_54_out, not_1_out, V, not_3_out, Y, Z);
  and and_55 (and_55_out, not_1_out, V, W, not_4_out, Y);
  and and_56 (and_56_out, not_1_out, V, W, X, not_5_out);
  and and_57 (and_57_out, U, not_2_out, not_3_out, Y);
  or or_1 (A, and_1_out, and_2_out, and_3_out, and_4_out, and_5_out, and_6_out, and_7_out, and_8_out, and_9_out);
  or or_2 (B, and_10_out, and_11_out, and_12_out, and_13_out, and_14_out, and_15_out, and_16_out, and_17_out, and_18_out);
  or or_3 (C, and_19_out, and_20_out, and_21_out, and_22_out, and_23_out, and_24_out, and_25_out, and_26_out, and_27_out, and_28_out);
  or or_4 (D, and_29_out, and_30_out, and_31_out, and_32_out, and_33_out, and_34_out, and_35_out, and_36_out, and_37_out, and_38_out);
  or or_5 (E, and_39_out, and_40_out, and_41_out, and_42_out, and_43_out, and_44_out, and_45_out, and_46_out, and_47_out);
  or or_6 (F, and_48_out, and_49_out, and_50_out, and_51_out, and_52_out, and_53_out, and_54_out, and_55_out, and_56_out, and_57_out);
endmodule

module Conversor (
  input  U,
  input  V,
  input  W,
  input  X,
  input  Y,
  input  Z,
  output A,
  output B,
  output C,
  output D,
  output E,
  output F
);

  wire and_1_out, and_2_out, and_3_out, and_4_out, and_5_out, and_6_out, and_7_out, and_8_out, and_9_out,
       and_10_out, and_11_out, and_12_out, and_13_out, and_14_out, and_15_out, and_16_out, and_17_out,
       and_18_out, and_19_out, and_20_out, and_21_out, and_22_out, and_23_out, and_24_out, and_25_out,
       and_26_out, and_27_out, and_28_out, and_29_out, and_30_out, and_31_out, and_32_out, and_33_out,
       and_34_out, and_35_out, and_36_out, and_37_out, and_38_out, and_39_out, and_40_out, and_41_out,
       and_42_out, and_43_out, and_44_out, and_45_out, and_46_out, and_47_out, and_48_out, and_49_out,
       and_50_out, and_51_out, and_52_out, and_53_out, and_54_out, and_55_out, and_56_out, and_57_out,
       and_58_out, and_59_out, and_60_out, and_61_out, and_62_out, and_63_out, and_64_out, and_65_out,
       and_66_out, and_67_out, and_68_out, and_69_out, and_70_out, and_71_out, and_72_out, and_73_out,
       and_74_out, and_75_out, and_76_out, and_77_out, and_78_out, and_79_out, and_80_out, not_1_out,
       not_2_out, not_3_out, not_4_out, not_5_out, not_6_out;

  not not_1 (not_1_out, U);
  not not_2 (not_2_out, V);
  not not_3 (not_3_out, W);
  not not_4 (not_4_out, X);
  not not_5 (not_5_out, Y);
  not not_6 (not_6_out, Z);
  and and_1 (and_1_out, not_2_out, not_3_out, Y, not_6_out);
  and and_2 (and_2_out, not_1_out, not_2_out, not_3_out, X, not_6_out);
  and and_3 (and_3_out, not_1_out, not_3_out, X, Y, not_6_out);
  and and_4 (and_4_out, not_2_out, W, not_4_out, not_5_out);
  and and_5 (and_5_out, not_1_out, not_2_out, W, not_5_out, Z);
  and and_6 (and_6_out, W, X, Y, Z);
  and and_7 (and_7_out, V, not_3_out, not_4_out, not_5_out);
  and and_8 (and_8_out, V, not_4_out, not_5_out, Z);
  and and_9 (and_9_out, not_1_out, V, W, not_6_out);
  and and_10 (and_10_out, U, not_2_out, not_4_out, Y);
  and and_11 (and_11_out, U, W, X, not_5_out, not_6_out);
  and and_12 (and_12_out, U, V, not_3_out, not_4_out, not_6_out);
  and and_13 (and_13_out, U, V, not_3_out, not_5_out, Z);
  and and_14 (and_14_out, not_1_out, not_2_out, not_3_out, not_5_out, Z);
  and and_15 (and_15_out, not_1_out, not_2_out, X, not_5_out, Z);
  and and_16 (and_16_out, not_1_out, not_2_out, X, Y, not_6_out);
  and and_17 (and_17_out, not_2_out, not_3_out, X, Y);
  and and_18 (and_18_out, not_1_out, V, not_4_out, not_5_out);
  and and_19 (and_19_out, not_1_out, V, not_3_out, not_4_out, Z);
  and and_20 (and_20_out, V, not_4_out, not_5_out, Z);
  and and_21 (and_21_out, V, not_3_out, X, not_6_out);
  and and_22 (and_22_out, V, W, not_4_out, Y, not_6_out);
  and and_23 (and_23_out, U, not_3_out, not_5_out, not_6_out);
  and and_24 (and_24_out, U, V, not_3_out, not_6_out);
  and and_25 (and_25_out, U, V, X);
  and and_26 (and_26_out, U, V, W, Y);
  and and_27 (and_27_out, not_1_out, not_3_out, not_4_out, not_5_out, not_6_out);
  and and_28 (and_28_out, not_1_out, not_3_out, not_4_out, Y, Z);
  and and_29 (and_29_out, not_2_out, not_3_out, X, Y);
  and and_30 (and_30_out, not_2_out, X, Y, not_6_out);
  and and_31 (and_31_out, not_1_out, V, not_3_out, not_5_out);
  and and_32 (and_32_out, V, not_3_out, not_4_out, Y, Z);
  and and_33 (and_33_out, not_1_out, V, W, Y, not_6_out);
  and and_34 (and_34_out, V, W, X, not_5_out, not_6_out);
  and and_35 (and_35_out, U, not_2_out, not_4_out, not_5_out, Z);
  and and_36 (and_36_out, U, not_2_out, Y, not_6_out);
  and and_37 (and_37_out, U, not_2_out, X, not_6_out);
  and and_38 (and_38_out, U, not_3_out, X, Y, not_6_out);
  and and_39 (and_39_out, U, W, Y, Z);
  and and_40 (and_40_out, U, not_2_out, W, X);
  and and_41 (and_41_out, U, V, W, not_4_out, not_5_out);
  and and_42 (and_42_out, not_1_out, not_2_out, not_3_out, Y, not_6_out);
  and and_43 (and_43_out, not_3_out, not_4_out, Y, Z);
  and and_44 (and_44_out, not_1_out, not_2_out, X, not_5_out, Z);
  and and_45 (and_45_out, not_2_out, not_3_out, X, Y, not_6_out);
  and and_46 (and_46_out, not_1_out, W, not_5_out, Z);
  and and_47 (and_47_out, not_1_out, W, X, not_6_out);
  and and_48 (and_48_out, V, X, not_5_out, not_6_out);
  and and_49 (and_49_out, not_1_out, V, W, not_5_out);
  and and_50 (and_50_out, not_1_out, V, W, not_4_out, Z);
  and and_51 (and_51_out, U, not_2_out, not_4_out, not_5_out, not_6_out);
  and and_52 (and_52_out, U, not_2_out, not_3_out, Z);
  and and_53 (and_53_out, U, not_3_out, X, Z);
  and and_54 (and_54_out, U, X, Y, Z);
  and and_55 (and_55_out, U, W, not_5_out, not_6_out);
  and and_56 (and_56_out, not_1_out, not_3_out, not_5_out, Z);
  and and_57 (and_57_out, not_1_out, not_4_out, not_5_out, Z);
  and and_58 (and_58_out, not_1_out, not_2_out, not_3_out, X, Z);
  and and_59 (and_59_out, not_2_out, W, Y);
  and and_60 (and_60_out, W, Y, Z);
  and and_61 (and_61_out, not_1_out, W, X, not_5_out, not_6_out);
  and and_62 (and_62_out, not_1_out, V, not_4_out, not_5_out);
  and and_63 (and_63_out, not_1_out, V, not_3_out, X, not_6_out);
  and and_64 (and_64_out, U, not_2_out, not_3_out, not_4_out, not_5_out);
  and and_65 (and_65_out, U, not_4_out, Y, Z);
  and and_66 (and_66_out, U, not_2_out, X, Y, not_6_out);
  and and_67 (and_67_out, U, W, X, Y);
  and and_68 (and_68_out, U, V, not_3_out, not_4_out, Y);
  and and_69 (and_69_out, not_4_out, not_5_out, Z);
  and and_70 (and_70_out, not_1_out, not_2_out, not_3_out, X);
  and and_71 (and_71_out, not_1_out, not_2_out, X, not_5_out, not_6_out);
  and and_72 (and_72_out, not_1_out, not_2_out, W, not_4_out, Y, not_6_out);
  and and_73 (and_73_out, not_1_out, V, not_3_out, not_4_out, Z);
  and and_74 (and_74_out, V, not_3_out, X, not_6_out);
  and and_75 (and_75_out, not_1_out, V, X, Y);
  and and_76 (and_76_out, U, not_5_out, Z);
  and and_77 (and_77_out, U, W, not_4_out, not_5_out);
  and and_78 (and_78_out, U, not_2_out, W, Z);
  and and_79 (and_79_out, U, W, X, Z);
  and and_80 (and_80_out, U, not_2_out, W, X, Y);
  or or_1 (A, and_1_out, and_2_out, and_3_out, and_4_out, and_5_out, and_6_out, and_7_out, and_8_out, and_9_out, and_10_out, and_11_out, and_12_out, and_13_out);
  or or_2 (B, and_14_out, and_15_out, and_16_out, and_17_out, and_18_out, and_19_out, and_20_out, and_21_out, and_22_out, and_23_out, and_24_out, and_25_out, and_26_out);
  or or_3 (C, and_27_out, and_28_out, and_29_out, and_30_out, and_31_out, and_32_out, and_33_out, and_34_out, and_35_out, and_36_out, and_37_out, and_38_out, and_39_out, and_40_out, and_41_out);
  or or_4 (D, and_42_out, and_43_out, and_44_out, and_45_out, and_46_out, and_47_out, and_48_out, and_49_out, and_50_out, and_51_out, and_52_out, and_53_out, and_54_out, and_55_out);
  or or_5 (E, and_56_out, and_57_out, and_58_out, and_59_out, and_60_out, and_61_out, and_62_out, and_63_out, and_64_out, and_65_out, and_66_out, and_67_out, and_68_out);
  or or_6 (F, and_69_out, and_70_out, and_71_out, and_72_out, and_73_out, and_74_out, and_75_out, and_76_out, and_77_out, and_78_out, and_79_out, and_80_out);
endmodule
